// Logisim project main.circ as structural Verilog: 11 circuits, main circuit main
module main (
);

  wire _0_clk, _1_clk, _2_clk, _3_clk, _4_clk, _5_clk, _6_clk, _7_clk, clk, controller_1_irq, down, flag,
       flag_clk, left, left_row, lose, open, open_clk, processor_hadnler_1_ack,
       processor_hadnler_1_st_row_out, reset, right, right_row, selected_0, selected_1, selected_2,
       selected_3, selected_4, selected_5, selected_6, selected_7, start, up, win;
  wire [2:0] controller_1_vec, selected_cell;
  wire [3:0] processor_hadnler_1_row_num;
  wire [6:0] row_drawer_1__00, row_drawer_1__01, row_drawer_1__02, row_drawer_1__03, row_drawer_1__04,
       row_drawer_1__05, row_drawer_1__06, row_drawer_1__07, row_drawer_1__10, row_drawer_1__11,
       row_drawer_1__12, row_drawer_1__13, row_drawer_1__14, row_drawer_1__15, row_drawer_1__16,
       row_drawer_1__17, row_drawer_1__20, row_drawer_1__21, row_drawer_1__22, row_drawer_1__23,
       row_drawer_1__24, row_drawer_1__25, row_drawer_1__26, row_drawer_1__27, row_drawer_1__30,
       row_drawer_1__31, row_drawer_1__32, row_drawer_1__33, row_drawer_1__34, row_drawer_1__35,
       row_drawer_1__36, row_drawer_1__37, row_drawer_1__40, row_drawer_1__41, row_drawer_1__42,
       row_drawer_1__43, row_drawer_1__44, row_drawer_1__45, row_drawer_1__46, row_drawer_1__47,
       row_drawer_1__50, row_drawer_1__51, row_drawer_1__52, row_drawer_1__53, row_drawer_1__54,
       row_drawer_1__55, row_drawer_1__56, row_drawer_1__57, row_drawer_1__60, row_drawer_1__61,
       row_drawer_1__62, row_drawer_1__63, row_drawer_1__64, row_drawer_1__65, row_drawer_1__66,
       row_drawer_1__67, row_drawer_1__70, row_drawer_1__71, row_drawer_1__72, row_drawer_1__73,
       row_drawer_1__74, row_drawer_1__75, row_drawer_1__76, row_drawer_1__77, row_drawer_2__00,
       row_drawer_2__01, row_drawer_2__02, row_drawer_2__03, row_drawer_2__04, row_drawer_2__05,
       row_drawer_2__06, row_drawer_2__07, row_drawer_2__10, row_drawer_2__11, row_drawer_2__12,
       row_drawer_2__13, row_drawer_2__14, row_drawer_2__15, row_drawer_2__16, row_drawer_2__17,
       row_drawer_2__20, row_drawer_2__21, row_drawer_2__22, row_drawer_2__23, row_drawer_2__24,
       row_drawer_2__25, row_drawer_2__26, row_drawer_2__27, row_drawer_2__30, row_drawer_2__31,
       row_drawer_2__32, row_drawer_2__33, row_drawer_2__34, row_drawer_2__35, row_drawer_2__36,
       row_drawer_2__37, row_drawer_2__40, row_drawer_2__41, row_drawer_2__42, row_drawer_2__43,
       row_drawer_2__44, row_drawer_2__45, row_drawer_2__46, row_drawer_2__47, row_drawer_2__50,
       row_drawer_2__51, row_drawer_2__52, row_drawer_2__53, row_drawer_2__54, row_drawer_2__55,
       row_drawer_2__56, row_drawer_2__57, row_drawer_2__60, row_drawer_2__61, row_drawer_2__62,
       row_drawer_2__63, row_drawer_2__64, row_drawer_2__65, row_drawer_2__66, row_drawer_2__67,
       row_drawer_2__70, row_drawer_2__71, row_drawer_2__72, row_drawer_2__73, row_drawer_2__74,
       row_drawer_2__75, row_drawer_2__76, row_drawer_2__77, row_drawer_3__00, row_drawer_3__01,
       row_drawer_3__02, row_drawer_3__03, row_drawer_3__04, row_drawer_3__05, row_drawer_3__06,
       row_drawer_3__07, row_drawer_3__10, row_drawer_3__11, row_drawer_3__12, row_drawer_3__13,
       row_drawer_3__14, row_drawer_3__15, row_drawer_3__16, row_drawer_3__17, row_drawer_3__20,
       row_drawer_3__21, row_drawer_3__22, row_drawer_3__23, row_drawer_3__24, row_drawer_3__25,
       row_drawer_3__26, row_drawer_3__27, row_drawer_3__30, row_drawer_3__31, row_drawer_3__32,
       row_drawer_3__33, row_drawer_3__34, row_drawer_3__35, row_drawer_3__36, row_drawer_3__37,
       row_drawer_3__40, row_drawer_3__41, row_drawer_3__42, row_drawer_3__43, row_drawer_3__44,
       row_drawer_3__45, row_drawer_3__46, row_drawer_3__47, row_drawer_3__50, row_drawer_3__51,
       row_drawer_3__52, row_drawer_3__53, row_drawer_3__54, row_drawer_3__55, row_drawer_3__56,
       row_drawer_3__57, row_drawer_3__60, row_drawer_3__61, row_drawer_3__62, row_drawer_3__63,
       row_drawer_3__64, row_drawer_3__65, row_drawer_3__66, row_drawer_3__67, row_drawer_3__70,
       row_drawer_3__71, row_drawer_3__72, row_drawer_3__73, row_drawer_3__74, row_drawer_3__75,
       row_drawer_3__76, row_drawer_3__77, row_drawer_4__00, row_drawer_4__01, row_drawer_4__02,
       row_drawer_4__03, row_drawer_4__04, row_drawer_4__05, row_drawer_4__06, row_drawer_4__07,
       row_drawer_4__10, row_drawer_4__11, row_drawer_4__12, row_drawer_4__13, row_drawer_4__14,
       row_drawer_4__15, row_drawer_4__16, row_drawer_4__17, row_drawer_4__20, row_drawer_4__21,
       row_drawer_4__22, row_drawer_4__23, row_drawer_4__24, row_drawer_4__25, row_drawer_4__26,
       row_drawer_4__27, row_drawer_4__30, row_drawer_4__31, row_drawer_4__32, row_drawer_4__33,
       row_drawer_4__34, row_drawer_4__35, row_drawer_4__36, row_drawer_4__37, row_drawer_4__40,
       row_drawer_4__41, row_drawer_4__42, row_drawer_4__43, row_drawer_4__44, row_drawer_4__45,
       row_drawer_4__46, row_drawer_4__47, row_drawer_4__50, row_drawer_4__51, row_drawer_4__52,
       row_drawer_4__53, row_drawer_4__54, row_drawer_4__55, row_drawer_4__56, row_drawer_4__57,
       row_drawer_4__60, row_drawer_4__61, row_drawer_4__62, row_drawer_4__63, row_drawer_4__64,
       row_drawer_4__65, row_drawer_4__66, row_drawer_4__67, row_drawer_4__70, row_drawer_4__71,
       row_drawer_4__72, row_drawer_4__73, row_drawer_4__74, row_drawer_4__75, row_drawer_4__76,
       row_drawer_4__77, row_drawer_5__00, row_drawer_5__01, row_drawer_5__02, row_drawer_5__03,
       row_drawer_5__04, row_drawer_5__05, row_drawer_5__06, row_drawer_5__07, row_drawer_5__10,
       row_drawer_5__11, row_drawer_5__12, row_drawer_5__13, row_drawer_5__14, row_drawer_5__15,
       row_drawer_5__16, row_drawer_5__17, row_drawer_5__20, row_drawer_5__21, row_drawer_5__22,
       row_drawer_5__23, row_drawer_5__24, row_drawer_5__25, row_drawer_5__26, row_drawer_5__27,
       row_drawer_5__30, row_drawer_5__31, row_drawer_5__32, row_drawer_5__33, row_drawer_5__34,
       row_drawer_5__35, row_drawer_5__36, row_drawer_5__37, row_drawer_5__40, row_drawer_5__41,
       row_drawer_5__42, row_drawer_5__43, row_drawer_5__44, row_drawer_5__45, row_drawer_5__46,
       row_drawer_5__47, row_drawer_5__50, row_drawer_5__51, row_drawer_5__52, row_drawer_5__53,
       row_drawer_5__54, row_drawer_5__55, row_drawer_5__56, row_drawer_5__57, row_drawer_5__60,
       row_drawer_5__61, row_drawer_5__62, row_drawer_5__63, row_drawer_5__64, row_drawer_5__65,
       row_drawer_5__66, row_drawer_5__67, row_drawer_5__70, row_drawer_5__71, row_drawer_5__72,
       row_drawer_5__73, row_drawer_5__74, row_drawer_5__75, row_drawer_5__76, row_drawer_5__77,
       row_drawer_6__00, row_drawer_6__01, row_drawer_6__02, row_drawer_6__03, row_drawer_6__04,
       row_drawer_6__05, row_drawer_6__06, row_drawer_6__07, row_drawer_6__10, row_drawer_6__11,
       row_drawer_6__12, row_drawer_6__13, row_drawer_6__14, row_drawer_6__15, row_drawer_6__16,
       row_drawer_6__17, row_drawer_6__20, row_drawer_6__21, row_drawer_6__22, row_drawer_6__23,
       row_drawer_6__24, row_drawer_6__25, row_drawer_6__26, row_drawer_6__27, row_drawer_6__30,
       row_drawer_6__31, row_drawer_6__32, row_drawer_6__33, row_drawer_6__34, row_drawer_6__35,
       row_drawer_6__36, row_drawer_6__37, row_drawer_6__40, row_drawer_6__41, row_drawer_6__42,
       row_drawer_6__43, row_drawer_6__44, row_drawer_6__45, row_drawer_6__46, row_drawer_6__47,
       row_drawer_6__50, row_drawer_6__51, row_drawer_6__52, row_drawer_6__53, row_drawer_6__54,
       row_drawer_6__55, row_drawer_6__56, row_drawer_6__57, row_drawer_6__60, row_drawer_6__61,
       row_drawer_6__62, row_drawer_6__63, row_drawer_6__64, row_drawer_6__65, row_drawer_6__66,
       row_drawer_6__67, row_drawer_6__70, row_drawer_6__71, row_drawer_6__72, row_drawer_6__73,
       row_drawer_6__74, row_drawer_6__75, row_drawer_6__76, row_drawer_6__77, row_drawer_7__00,
       row_drawer_7__01, row_drawer_7__02, row_drawer_7__03, row_drawer_7__04, row_drawer_7__05,
       row_drawer_7__06, row_drawer_7__07, row_drawer_7__10, row_drawer_7__11, row_drawer_7__12,
       row_drawer_7__13, row_drawer_7__14, row_drawer_7__15, row_drawer_7__16, row_drawer_7__17,
       row_drawer_7__20, row_drawer_7__21, row_drawer_7__22, row_drawer_7__23, row_drawer_7__24,
       row_drawer_7__25, row_drawer_7__26, row_drawer_7__27, row_drawer_7__30, row_drawer_7__31,
       row_drawer_7__32, row_drawer_7__33, row_drawer_7__34, row_drawer_7__35, row_drawer_7__36,
       row_drawer_7__37, row_drawer_7__40, row_drawer_7__41, row_drawer_7__42, row_drawer_7__43,
       row_drawer_7__44, row_drawer_7__45, row_drawer_7__46, row_drawer_7__47, row_drawer_7__50,
       row_drawer_7__51, row_drawer_7__52, row_drawer_7__53, row_drawer_7__54, row_drawer_7__55,
       row_drawer_7__56, row_drawer_7__57, row_drawer_7__60, row_drawer_7__61, row_drawer_7__62,
       row_drawer_7__63, row_drawer_7__64, row_drawer_7__65, row_drawer_7__66, row_drawer_7__67,
       row_drawer_7__70, row_drawer_7__71, row_drawer_7__72, row_drawer_7__73, row_drawer_7__74,
       row_drawer_7__75, row_drawer_7__76, row_drawer_7__77, row_drawer_8__00, row_drawer_8__01,
       row_drawer_8__02, row_drawer_8__03, row_drawer_8__04, row_drawer_8__05, row_drawer_8__06,
       row_drawer_8__07, row_drawer_8__10, row_drawer_8__11, row_drawer_8__12, row_drawer_8__13,
       row_drawer_8__14, row_drawer_8__15, row_drawer_8__16, row_drawer_8__17, row_drawer_8__20,
       row_drawer_8__21, row_drawer_8__22, row_drawer_8__23, row_drawer_8__24, row_drawer_8__25,
       row_drawer_8__26, row_drawer_8__27, row_drawer_8__30, row_drawer_8__31, row_drawer_8__32,
       row_drawer_8__33, row_drawer_8__34, row_drawer_8__35, row_drawer_8__36, row_drawer_8__37,
       row_drawer_8__40, row_drawer_8__41, row_drawer_8__42, row_drawer_8__43, row_drawer_8__44,
       row_drawer_8__45, row_drawer_8__46, row_drawer_8__47, row_drawer_8__50, row_drawer_8__51,
       row_drawer_8__52, row_drawer_8__53, row_drawer_8__54, row_drawer_8__55, row_drawer_8__56,
       row_drawer_8__57, row_drawer_8__60, row_drawer_8__61, row_drawer_8__62, row_drawer_8__63,
       row_drawer_8__64, row_drawer_8__65, row_drawer_8__66, row_drawer_8__67, row_drawer_8__70,
       row_drawer_8__71, row_drawer_8__72, row_drawer_8__73, row_drawer_8__74, row_drawer_8__75,
       row_drawer_8__76, row_drawer_8__77;
  wire [7:0] f_out_0, f_out_1, f_out_2, f_out_3, f_out_4, f_out_5, f_out_6, f_out_7, flags, or_1_out,
       or_2_out, or_3_out, or_4_out, or_5_out, or_6_out, processor_hadnler_1_selected;
  wire [13:0] info_display_1__00, info_display_1__00_2, info_display_1__00_3, info_display_1__00_4,
       info_display_1__00_5, info_display_1__00_6, info_display_1__00_7, info_display_1__00_8,
       info_display_1__00_9, info_display_1__00_10, info_display_1__00_11, info_display_1__00_12,
       info_display_1__00_13, info_display_1__00_14, info_display_1__00_15, info_display_1__00_16,
       info_display_1__00_17, info_display_1__00_18, info_display_1__00_19, info_display_1__00_20,
       info_display_1__01, info_display_1__01_2, info_display_1__01_3, info_display_1__01_4,
       info_display_1__01_5, info_display_1__01_6, info_display_1__01_7, info_display_1__01_8,
       info_display_1__01_9, info_display_1__01_10, info_display_1__01_11, info_display_1__01_12,
       info_display_1__01_13, info_display_1__01_14, info_display_1__01_15, info_display_1__01_16,
       info_display_1__01_17, info_display_1__01_18, info_display_1__01_19, info_display_1__01_20;
  wire [31:0] row_data;

  Button button (.out(up));
  Button v (.out(down));
  Button button_2 (.out(left));
  Button S (.out(start));
  Button R (.out(reset));
  Button button_3 (.out(right));
  Button F (.out(flag));
  Button O (.out(open));
  controller controller_1 (
    .reset(reset), .up(up), .left(left), .down(down), .right(right), .open(open), .flag(flag),
    .IRQ(controller_1_irq), .vec(controller_1_vec), .clk(clk), .IAck(processor_hadnler_1_ack), .start(start),
    .win(win), .lose(lose));
  processor_hadnler processor_hadnler_1 (
    .row_out(row_data), .row_num(processor_hadnler_1_row_num), .IRQ(controller_1_irq),
    .vec(controller_1_vec), .st_row_out(processor_hadnler_1_st_row_out), .clk(clk), .reset(reset),
    .selected(processor_hadnler_1_selected), .Ack(processor_hadnler_1_ack), .flag(flag_clk), .open(open_clk),
    .start(start), .win(win), .lose(lose), .flags(flags));
  Clock clock_1 (.out(clk));
  Info_display info_display_1 (
    .win(win), .lose(lose), .reset(reset), .start(start), .flags(flags), ._00_5(info_display_1__00_5),
    ._01_5(info_display_1__01_5), ._00_10(info_display_1__00_10), ._01_10(info_display_1__01_10),
    ._00_15(info_display_1__00_15), ._01_15(info_display_1__01_15), ._00_20(info_display_1__00_20),
    ._01_20(info_display_1__01_20), ._00(info_display_1__00), ._01(info_display_1__01),
    ._00_6(info_display_1__00_6), ._01_6(info_display_1__01_6), ._00_11(info_display_1__00_11),
    ._01_11(info_display_1__01_11), ._00_16(info_display_1__00_16), ._01_16(info_display_1__01_16),
    ._00_2(info_display_1__00_2), ._01_2(info_display_1__01_2), ._00_7(info_display_1__00_7),
    ._01_7(info_display_1__01_7), ._00_12(info_display_1__00_12), ._01_12(info_display_1__01_12),
    ._00_17(info_display_1__00_17), ._01_17(info_display_1__01_17), ._00_3(info_display_1__00_3),
    ._01_3(info_display_1__01_3), ._00_8(info_display_1__00_8), ._01_8(info_display_1__01_8),
    ._00_13(info_display_1__00_13), ._01_13(info_display_1__01_13), ._00_18(info_display_1__00_18),
    ._01_18(info_display_1__01_18), ._00_4(info_display_1__00_4), ._01_4(info_display_1__01_4),
    ._00_9(info_display_1__00_9), ._01_9(info_display_1__01_9), ._00_14(info_display_1__00_14),
    ._01_14(info_display_1__01_14), ._00_19(info_display_1__00_19), ._01_19(info_display_1__01_19));
  DotMatrix #(.matrixcols(8)) dotmatrix_1 (
    .col0(row_drawer_1__00), .col1(row_drawer_1__01), .col2(row_drawer_1__02), .col3(row_drawer_1__03),
    .col4(row_drawer_1__04), .col5(row_drawer_1__05), .col6(row_drawer_1__06), .col7(row_drawer_1__07));
  row_drawer row_drawer_1 (
    ._00(row_drawer_1__00), ._01(row_drawer_1__01), ._02(row_drawer_1__02), ._03(row_drawer_1__03),
    ._04(row_drawer_1__04), ._05(row_drawer_1__05), ._06(row_drawer_1__06), ._07(row_drawer_1__07),
    ._10(row_drawer_1__10), ._11(row_drawer_1__11), ._12(row_drawer_1__12), ._13(row_drawer_1__13),
    ._14(row_drawer_1__14), ._15(row_drawer_1__15), ._16(row_drawer_1__16), ._17(row_drawer_1__17),
    ._20(row_drawer_1__20), ._21(row_drawer_1__21), ._22(row_drawer_1__22), ._23(row_drawer_1__23),
    ._24(row_drawer_1__24), ._25(row_drawer_1__25), ._26(row_drawer_1__26), ._27(row_drawer_1__27),
    ._30(row_drawer_1__30), ._31(row_drawer_1__31), ._32(row_drawer_1__32), ._33(row_drawer_1__33),
    ._34(row_drawer_1__34), ._35(row_drawer_1__35), ._36(row_drawer_1__36), ._37(row_drawer_1__37),
    ._60(row_drawer_1__60), ._61(row_drawer_1__61), ._62(row_drawer_1__62), ._63(row_drawer_1__63),
    ._64(row_drawer_1__64), ._65(row_drawer_1__65), ._66(row_drawer_1__66), ._67(row_drawer_1__67),
    ._70(row_drawer_1__70), ._40(row_drawer_1__40), ._71(row_drawer_1__71), ._41(row_drawer_1__41),
    ._72(row_drawer_1__72), ._42(row_drawer_1__42), ._73(row_drawer_1__73), ._43(row_drawer_1__43),
    ._74(row_drawer_1__74), ._44(row_drawer_1__44), ._75(row_drawer_1__75), ._45(row_drawer_1__45),
    ._76(row_drawer_1__76), ._46(row_drawer_1__46), ._77(row_drawer_1__77), ._47(row_drawer_1__47),
    ._50(row_drawer_1__50), ._51(row_drawer_1__51), ._52(row_drawer_1__52), ._53(row_drawer_1__53),
    ._54(row_drawer_1__54), ._55(row_drawer_1__55), ._56(row_drawer_1__56), ._57(row_drawer_1__57),
    .clk(_0_clk), .left(left_row), .right(right_row), .data(row_data), .selected(selected_0),
    .selected_cell(selected_cell), .open(open_clk), .flag(flag_clk), .force_out(f_out_0), .force_in(f_out_1),
    .reset(reset));
  DotMatrix #(.matrixcols(8)) dotmatrix_2 (
    .col0(row_drawer_2__00), .col1(row_drawer_2__01), .col2(row_drawer_2__02), .col3(row_drawer_2__03),
    .col4(row_drawer_2__04), .col5(row_drawer_2__05), .col6(row_drawer_2__06), .col7(row_drawer_2__07));
  row_drawer row_drawer_2 (
    ._00(row_drawer_2__00), ._01(row_drawer_2__01), ._02(row_drawer_2__02), ._03(row_drawer_2__03),
    ._04(row_drawer_2__04), ._05(row_drawer_2__05), ._06(row_drawer_2__06), ._07(row_drawer_2__07),
    ._10(row_drawer_2__10), ._11(row_drawer_2__11), ._12(row_drawer_2__12), ._13(row_drawer_2__13),
    ._14(row_drawer_2__14), ._15(row_drawer_2__15), ._16(row_drawer_2__16), ._17(row_drawer_2__17),
    ._20(row_drawer_2__20), ._21(row_drawer_2__21), ._22(row_drawer_2__22), ._23(row_drawer_2__23),
    ._24(row_drawer_2__24), ._25(row_drawer_2__25), ._26(row_drawer_2__26), ._27(row_drawer_2__27),
    ._30(row_drawer_2__30), ._31(row_drawer_2__31), ._32(row_drawer_2__32), ._33(row_drawer_2__33),
    ._34(row_drawer_2__34), ._35(row_drawer_2__35), ._36(row_drawer_2__36), ._37(row_drawer_2__37),
    ._60(row_drawer_2__60), ._61(row_drawer_2__61), ._62(row_drawer_2__62), ._63(row_drawer_2__63),
    ._64(row_drawer_2__64), ._65(row_drawer_2__65), ._66(row_drawer_2__66), ._67(row_drawer_2__67),
    ._70(row_drawer_2__70), ._40(row_drawer_2__40), ._71(row_drawer_2__71), ._41(row_drawer_2__41),
    ._72(row_drawer_2__72), ._42(row_drawer_2__42), ._73(row_drawer_2__73), ._43(row_drawer_2__43),
    ._74(row_drawer_2__74), ._44(row_drawer_2__44), ._75(row_drawer_2__75), ._45(row_drawer_2__45),
    ._76(row_drawer_2__76), ._46(row_drawer_2__46), ._77(row_drawer_2__77), ._47(row_drawer_2__47),
    ._50(row_drawer_2__50), ._51(row_drawer_2__51), ._52(row_drawer_2__52), ._53(row_drawer_2__53),
    ._54(row_drawer_2__54), ._55(row_drawer_2__55), ._56(row_drawer_2__56), ._57(row_drawer_2__57),
    .clk(_1_clk), .left(left_row), .right(right_row), .data(row_data), .selected(selected_1),
    .selected_cell(selected_cell), .open(open_clk), .flag(flag_clk), .force_out(f_out_1),
    .force_in(or_1_out), .reset(reset));
  DotMatrix #(.matrixcols(8)) dotmatrix_3 (
    .col0(row_drawer_3__00), .col1(row_drawer_3__01), .col2(row_drawer_3__02), .col3(row_drawer_3__03),
    .col4(row_drawer_3__04), .col5(row_drawer_3__05), .col6(row_drawer_3__06), .col7(row_drawer_3__07));
  row_drawer row_drawer_3 (
    ._00(row_drawer_3__00), ._01(row_drawer_3__01), ._02(row_drawer_3__02), ._03(row_drawer_3__03),
    ._04(row_drawer_3__04), ._05(row_drawer_3__05), ._06(row_drawer_3__06), ._07(row_drawer_3__07),
    ._10(row_drawer_3__10), ._11(row_drawer_3__11), ._12(row_drawer_3__12), ._13(row_drawer_3__13),
    ._14(row_drawer_3__14), ._15(row_drawer_3__15), ._16(row_drawer_3__16), ._17(row_drawer_3__17),
    ._20(row_drawer_3__20), ._21(row_drawer_3__21), ._22(row_drawer_3__22), ._23(row_drawer_3__23),
    ._24(row_drawer_3__24), ._25(row_drawer_3__25), ._26(row_drawer_3__26), ._27(row_drawer_3__27),
    ._30(row_drawer_3__30), ._31(row_drawer_3__31), ._32(row_drawer_3__32), ._33(row_drawer_3__33),
    ._34(row_drawer_3__34), ._35(row_drawer_3__35), ._36(row_drawer_3__36), ._37(row_drawer_3__37),
    ._60(row_drawer_3__60), ._61(row_drawer_3__61), ._62(row_drawer_3__62), ._63(row_drawer_3__63),
    ._64(row_drawer_3__64), ._65(row_drawer_3__65), ._66(row_drawer_3__66), ._67(row_drawer_3__67),
    ._70(row_drawer_3__70), ._40(row_drawer_3__40), ._71(row_drawer_3__71), ._41(row_drawer_3__41),
    ._72(row_drawer_3__72), ._42(row_drawer_3__42), ._73(row_drawer_3__73), ._43(row_drawer_3__43),
    ._74(row_drawer_3__74), ._44(row_drawer_3__44), ._75(row_drawer_3__75), ._45(row_drawer_3__45),
    ._76(row_drawer_3__76), ._46(row_drawer_3__46), ._77(row_drawer_3__77), ._47(row_drawer_3__47),
    ._50(row_drawer_3__50), ._51(row_drawer_3__51), ._52(row_drawer_3__52), ._53(row_drawer_3__53),
    ._54(row_drawer_3__54), ._55(row_drawer_3__55), ._56(row_drawer_3__56), ._57(row_drawer_3__57),
    .clk(_2_clk), .left(left_row), .right(right_row), .data(row_data), .selected(selected_2),
    .selected_cell(selected_cell), .open(open_clk), .flag(flag_clk), .force_out(f_out_2),
    .force_in(or_2_out), .reset(reset));
  DotMatrix #(.matrixcols(8)) dotmatrix_4 (
    .col0(row_drawer_4__00), .col1(row_drawer_4__01), .col2(row_drawer_4__02), .col3(row_drawer_4__03),
    .col4(row_drawer_4__04), .col5(row_drawer_4__05), .col6(row_drawer_4__06), .col7(row_drawer_4__07));
  row_drawer row_drawer_4 (
    ._00(row_drawer_4__00), ._01(row_drawer_4__01), ._02(row_drawer_4__02), ._03(row_drawer_4__03),
    ._04(row_drawer_4__04), ._05(row_drawer_4__05), ._06(row_drawer_4__06), ._07(row_drawer_4__07),
    ._10(row_drawer_4__10), ._11(row_drawer_4__11), ._12(row_drawer_4__12), ._13(row_drawer_4__13),
    ._14(row_drawer_4__14), ._15(row_drawer_4__15), ._16(row_drawer_4__16), ._17(row_drawer_4__17),
    ._20(row_drawer_4__20), ._21(row_drawer_4__21), ._22(row_drawer_4__22), ._23(row_drawer_4__23),
    ._24(row_drawer_4__24), ._25(row_drawer_4__25), ._26(row_drawer_4__26), ._27(row_drawer_4__27),
    ._30(row_drawer_4__30), ._31(row_drawer_4__31), ._32(row_drawer_4__32), ._33(row_drawer_4__33),
    ._34(row_drawer_4__34), ._35(row_drawer_4__35), ._36(row_drawer_4__36), ._37(row_drawer_4__37),
    ._60(row_drawer_4__60), ._61(row_drawer_4__61), ._62(row_drawer_4__62), ._63(row_drawer_4__63),
    ._64(row_drawer_4__64), ._65(row_drawer_4__65), ._66(row_drawer_4__66), ._67(row_drawer_4__67),
    ._70(row_drawer_4__70), ._40(row_drawer_4__40), ._71(row_drawer_4__71), ._41(row_drawer_4__41),
    ._72(row_drawer_4__72), ._42(row_drawer_4__42), ._73(row_drawer_4__73), ._43(row_drawer_4__43),
    ._74(row_drawer_4__74), ._44(row_drawer_4__44), ._75(row_drawer_4__75), ._45(row_drawer_4__45),
    ._76(row_drawer_4__76), ._46(row_drawer_4__46), ._77(row_drawer_4__77), ._47(row_drawer_4__47),
    ._50(row_drawer_4__50), ._51(row_drawer_4__51), ._52(row_drawer_4__52), ._53(row_drawer_4__53),
    ._54(row_drawer_4__54), ._55(row_drawer_4__55), ._56(row_drawer_4__56), ._57(row_drawer_4__57),
    .clk(_3_clk), .left(left_row), .right(right_row), .data(row_data), .selected(selected_3),
    .selected_cell(selected_cell), .open(open_clk), .flag(flag_clk), .force_out(f_out_3),
    .force_in(or_3_out), .reset(reset));
  row_drawer row_drawer_5 (
    ._00(row_drawer_5__00), ._01(row_drawer_5__01), ._02(row_drawer_5__02), ._03(row_drawer_5__03),
    ._04(row_drawer_5__04), ._05(row_drawer_5__05), ._06(row_drawer_5__06), ._07(row_drawer_5__07),
    ._10(row_drawer_5__10), ._11(row_drawer_5__11), ._12(row_drawer_5__12), ._13(row_drawer_5__13),
    ._14(row_drawer_5__14), ._15(row_drawer_5__15), ._16(row_drawer_5__16), ._17(row_drawer_5__17),
    ._20(row_drawer_5__20), ._21(row_drawer_5__21), ._22(row_drawer_5__22), ._23(row_drawer_5__23),
    ._24(row_drawer_5__24), ._25(row_drawer_5__25), ._26(row_drawer_5__26), ._27(row_drawer_5__27),
    ._30(row_drawer_5__30), ._31(row_drawer_5__31), ._32(row_drawer_5__32), ._33(row_drawer_5__33),
    ._34(row_drawer_5__34), ._35(row_drawer_5__35), ._36(row_drawer_5__36), ._37(row_drawer_5__37),
    ._60(row_drawer_5__60), ._61(row_drawer_5__61), ._62(row_drawer_5__62), ._63(row_drawer_5__63),
    ._64(row_drawer_5__64), ._65(row_drawer_5__65), ._66(row_drawer_5__66), ._67(row_drawer_5__67),
    ._70(row_drawer_5__70), ._40(row_drawer_5__40), ._71(row_drawer_5__71), ._41(row_drawer_5__41),
    ._72(row_drawer_5__72), ._42(row_drawer_5__42), ._73(row_drawer_5__73), ._43(row_drawer_5__43),
    ._74(row_drawer_5__74), ._44(row_drawer_5__44), ._75(row_drawer_5__75), ._45(row_drawer_5__45),
    ._76(row_drawer_5__76), ._46(row_drawer_5__46), ._77(row_drawer_5__77), ._47(row_drawer_5__47),
    ._50(row_drawer_5__50), ._51(row_drawer_5__51), ._52(row_drawer_5__52), ._53(row_drawer_5__53),
    ._54(row_drawer_5__54), ._55(row_drawer_5__55), ._56(row_drawer_5__56), ._57(row_drawer_5__57),
    .clk(_4_clk), .left(left_row), .right(right_row), .data(row_data), .selected(selected_4),
    .selected_cell(selected_cell), .open(open_clk), .flag(flag_clk), .force_out(f_out_4),
    .force_in(or_4_out), .reset(reset));
  DotMatrix #(.matrixcols(8)) dotmatrix_5 (
    .col0(row_drawer_5__00), .col1(row_drawer_5__01), .col2(row_drawer_5__02), .col3(row_drawer_5__03),
    .col4(row_drawer_5__04), .col5(row_drawer_5__05), .col6(row_drawer_5__06), .col7(row_drawer_5__07));
  row_drawer row_drawer_6 (
    ._00(row_drawer_6__00), ._01(row_drawer_6__01), ._02(row_drawer_6__02), ._03(row_drawer_6__03),
    ._04(row_drawer_6__04), ._05(row_drawer_6__05), ._06(row_drawer_6__06), ._07(row_drawer_6__07),
    ._10(row_drawer_6__10), ._11(row_drawer_6__11), ._12(row_drawer_6__12), ._13(row_drawer_6__13),
    ._14(row_drawer_6__14), ._15(row_drawer_6__15), ._16(row_drawer_6__16), ._17(row_drawer_6__17),
    ._20(row_drawer_6__20), ._21(row_drawer_6__21), ._22(row_drawer_6__22), ._23(row_drawer_6__23),
    ._24(row_drawer_6__24), ._25(row_drawer_6__25), ._26(row_drawer_6__26), ._27(row_drawer_6__27),
    ._30(row_drawer_6__30), ._31(row_drawer_6__31), ._32(row_drawer_6__32), ._33(row_drawer_6__33),
    ._34(row_drawer_6__34), ._35(row_drawer_6__35), ._36(row_drawer_6__36), ._37(row_drawer_6__37),
    ._60(row_drawer_6__60), ._61(row_drawer_6__61), ._62(row_drawer_6__62), ._63(row_drawer_6__63),
    ._64(row_drawer_6__64), ._65(row_drawer_6__65), ._66(row_drawer_6__66), ._67(row_drawer_6__67),
    ._70(row_drawer_6__70), ._40(row_drawer_6__40), ._71(row_drawer_6__71), ._41(row_drawer_6__41),
    ._72(row_drawer_6__72), ._42(row_drawer_6__42), ._73(row_drawer_6__73), ._43(row_drawer_6__43),
    ._74(row_drawer_6__74), ._44(row_drawer_6__44), ._75(row_drawer_6__75), ._45(row_drawer_6__45),
    ._76(row_drawer_6__76), ._46(row_drawer_6__46), ._77(row_drawer_6__77), ._47(row_drawer_6__47),
    ._50(row_drawer_6__50), ._51(row_drawer_6__51), ._52(row_drawer_6__52), ._53(row_drawer_6__53),
    ._54(row_drawer_6__54), ._55(row_drawer_6__55), ._56(row_drawer_6__56), ._57(row_drawer_6__57),
    .clk(_5_clk), .left(left_row), .right(right_row), .data(row_data), .selected(selected_5),
    .selected_cell(selected_cell), .open(open_clk), .flag(flag_clk), .force_out(f_out_5),
    .force_in(or_5_out), .reset(reset));
  DotMatrix #(.matrixcols(8)) dotmatrix_6 (
    .col0(row_drawer_6__00), .col1(row_drawer_6__01), .col2(row_drawer_6__02), .col3(row_drawer_6__03),
    .col4(row_drawer_6__04), .col5(row_drawer_6__05), .col6(row_drawer_6__06), .col7(row_drawer_6__07));
  DotMatrix #(.matrixcols(8)) dotmatrix_7 (
    .col0(row_drawer_7__00), .col1(row_drawer_7__01), .col2(row_drawer_7__02), .col3(row_drawer_7__03),
    .col4(row_drawer_7__04), .col5(row_drawer_7__05), .col6(row_drawer_7__06), .col7(row_drawer_7__07));
  row_drawer row_drawer_7 (
    ._00(row_drawer_7__00), ._01(row_drawer_7__01), ._02(row_drawer_7__02), ._03(row_drawer_7__03),
    ._04(row_drawer_7__04), ._05(row_drawer_7__05), ._06(row_drawer_7__06), ._07(row_drawer_7__07),
    ._10(row_drawer_7__10), ._11(row_drawer_7__11), ._12(row_drawer_7__12), ._13(row_drawer_7__13),
    ._14(row_drawer_7__14), ._15(row_drawer_7__15), ._16(row_drawer_7__16), ._17(row_drawer_7__17),
    ._20(row_drawer_7__20), ._21(row_drawer_7__21), ._22(row_drawer_7__22), ._23(row_drawer_7__23),
    ._24(row_drawer_7__24), ._25(row_drawer_7__25), ._26(row_drawer_7__26), ._27(row_drawer_7__27),
    ._30(row_drawer_7__30), ._31(row_drawer_7__31), ._32(row_drawer_7__32), ._33(row_drawer_7__33),
    ._34(row_drawer_7__34), ._35(row_drawer_7__35), ._36(row_drawer_7__36), ._37(row_drawer_7__37),
    ._60(row_drawer_7__60), ._61(row_drawer_7__61), ._62(row_drawer_7__62), ._63(row_drawer_7__63),
    ._64(row_drawer_7__64), ._65(row_drawer_7__65), ._66(row_drawer_7__66), ._67(row_drawer_7__67),
    ._70(row_drawer_7__70), ._40(row_drawer_7__40), ._71(row_drawer_7__71), ._41(row_drawer_7__41),
    ._72(row_drawer_7__72), ._42(row_drawer_7__42), ._73(row_drawer_7__73), ._43(row_drawer_7__43),
    ._74(row_drawer_7__74), ._44(row_drawer_7__44), ._75(row_drawer_7__75), ._45(row_drawer_7__45),
    ._76(row_drawer_7__76), ._46(row_drawer_7__46), ._77(row_drawer_7__77), ._47(row_drawer_7__47),
    ._50(row_drawer_7__50), ._51(row_drawer_7__51), ._52(row_drawer_7__52), ._53(row_drawer_7__53),
    ._54(row_drawer_7__54), ._55(row_drawer_7__55), ._56(row_drawer_7__56), ._57(row_drawer_7__57),
    .clk(_6_clk), .left(left_row), .right(right_row), .data(row_data), .selected(selected_6),
    .selected_cell(selected_cell), .open(open_clk), .flag(flag_clk), .force_out(f_out_6),
    .force_in(or_6_out), .reset(reset));
  row_drawer row_drawer_8 (
    ._00(row_drawer_8__00), ._01(row_drawer_8__01), ._02(row_drawer_8__02), ._03(row_drawer_8__03),
    ._04(row_drawer_8__04), ._05(row_drawer_8__05), ._06(row_drawer_8__06), ._07(row_drawer_8__07),
    ._10(row_drawer_8__10), ._11(row_drawer_8__11), ._12(row_drawer_8__12), ._13(row_drawer_8__13),
    ._14(row_drawer_8__14), ._15(row_drawer_8__15), ._16(row_drawer_8__16), ._17(row_drawer_8__17),
    ._20(row_drawer_8__20), ._21(row_drawer_8__21), ._22(row_drawer_8__22), ._23(row_drawer_8__23),
    ._24(row_drawer_8__24), ._25(row_drawer_8__25), ._26(row_drawer_8__26), ._27(row_drawer_8__27),
    ._30(row_drawer_8__30), ._31(row_drawer_8__31), ._32(row_drawer_8__32), ._33(row_drawer_8__33),
    ._34(row_drawer_8__34), ._35(row_drawer_8__35), ._36(row_drawer_8__36), ._37(row_drawer_8__37),
    ._60(row_drawer_8__60), ._61(row_drawer_8__61), ._62(row_drawer_8__62), ._63(row_drawer_8__63),
    ._64(row_drawer_8__64), ._65(row_drawer_8__65), ._66(row_drawer_8__66), ._67(row_drawer_8__67),
    ._70(row_drawer_8__70), ._40(row_drawer_8__40), ._71(row_drawer_8__71), ._41(row_drawer_8__41),
    ._72(row_drawer_8__72), ._42(row_drawer_8__42), ._73(row_drawer_8__73), ._43(row_drawer_8__43),
    ._74(row_drawer_8__74), ._44(row_drawer_8__44), ._75(row_drawer_8__75), ._45(row_drawer_8__45),
    ._76(row_drawer_8__76), ._46(row_drawer_8__46), ._77(row_drawer_8__77), ._47(row_drawer_8__47),
    ._50(row_drawer_8__50), ._51(row_drawer_8__51), ._52(row_drawer_8__52), ._53(row_drawer_8__53),
    ._54(row_drawer_8__54), ._55(row_drawer_8__55), ._56(row_drawer_8__56), ._57(row_drawer_8__57),
    .clk(_7_clk), .left(left_row), .right(right_row), .data(row_data), .selected(selected_7),
    .selected_cell(selected_cell), .open(open_clk), .flag(flag_clk), .force_out(f_out_7), .force_in(f_out_6),
    .reset(reset));
  DotMatrix #(.matrixcols(8)) dotmatrix_8 (
    .col0(row_drawer_8__00), .col1(row_drawer_8__01), .col2(row_drawer_8__02), .col3(row_drawer_8__03),
    .col4(row_drawer_8__04), .col5(row_drawer_8__05), .col6(row_drawer_8__06), .col7(row_drawer_8__07));
  DotMatrix #(.matrixcols(32), .matrixrows(14)) dotmatrix_9 (
    .col0(info_display_1__00_5), .col1(info_display_1__01_5), .col2(info_display_1__00_10),
    .col3(info_display_1__01_10), .col4(info_display_1__00_15), .col5(info_display_1__01_15),
    .col6(info_display_1__00_20), .col7(info_display_1__01_20), .col8(info_display_1__00),
    .col9(info_display_1__01), .col10(info_display_1__00_6), .col11(info_display_1__01_6),
    .col12(info_display_1__00_11), .col13(info_display_1__01_11), .col14(info_display_1__00_16),
    .col15(info_display_1__01_16), .col16(info_display_1__00_2), .col17(info_display_1__01_2),
    .col18(info_display_1__00_7), .col19(info_display_1__01_7), .col20(info_display_1__00_12),
    .col21(info_display_1__01_12), .col22(info_display_1__00_17), .col23(info_display_1__01_17),
    .col24(info_display_1__00_3), .col25(info_display_1__01_3), .col26(info_display_1__00_8),
    .col27(info_display_1__01_8), .col28(info_display_1__00_13), .col29(info_display_1__01_13),
    .col30(info_display_1__00_18), .col31(info_display_1__01_18));
  DotMatrix #(.matrixcols(8)) dotmatrix_10 (
    .col0(row_drawer_1__10), .col1(row_drawer_1__11), .col2(row_drawer_1__12), .col3(row_drawer_1__13),
    .col4(row_drawer_1__14), .col5(row_drawer_1__15), .col6(row_drawer_1__16), .col7(row_drawer_1__17));
  DotMatrix #(.matrixcols(8)) dotmatrix_11 (
    .col0(row_drawer_2__10), .col1(row_drawer_2__11), .col2(row_drawer_2__12), .col3(row_drawer_2__13),
    .col4(row_drawer_2__14), .col5(row_drawer_2__15), .col6(row_drawer_2__16), .col7(row_drawer_2__17));
  DotMatrix #(.matrixcols(8)) dotmatrix_12 (
    .col0(row_drawer_3__10), .col1(row_drawer_3__11), .col2(row_drawer_3__12), .col3(row_drawer_3__13),
    .col4(row_drawer_3__14), .col5(row_drawer_3__15), .col6(row_drawer_3__16), .col7(row_drawer_3__17));
  DotMatrix #(.matrixcols(8)) dotmatrix_13 (
    .col0(row_drawer_4__10), .col1(row_drawer_4__11), .col2(row_drawer_4__12), .col3(row_drawer_4__13),
    .col4(row_drawer_4__14), .col5(row_drawer_4__15), .col6(row_drawer_4__16), .col7(row_drawer_4__17));
  DotMatrix #(.matrixcols(8)) dotmatrix_14 (
    .col0(row_drawer_5__10), .col1(row_drawer_5__11), .col2(row_drawer_5__12), .col3(row_drawer_5__13),
    .col4(row_drawer_5__14), .col5(row_drawer_5__15), .col6(row_drawer_5__16), .col7(row_drawer_5__17));
  DotMatrix #(.matrixcols(8)) dotmatrix_15 (
    .col0(row_drawer_6__10), .col1(row_drawer_6__11), .col2(row_drawer_6__12), .col3(row_drawer_6__13),
    .col4(row_drawer_6__14), .col5(row_drawer_6__15), .col6(row_drawer_6__16), .col7(row_drawer_6__17));
  DotMatrix #(.matrixcols(8)) dotmatrix_16 (
    .col0(row_drawer_7__10), .col1(row_drawer_7__11), .col2(row_drawer_7__12), .col3(row_drawer_7__13),
    .col4(row_drawer_7__14), .col5(row_drawer_7__15), .col6(row_drawer_7__16), .col7(row_drawer_7__17));
  DotMatrix #(.matrixcols(8)) dotmatrix_17 (
    .col0(row_drawer_8__10), .col1(row_drawer_8__11), .col2(row_drawer_8__12), .col3(row_drawer_8__13),
    .col4(row_drawer_8__14), .col5(row_drawer_8__15), .col6(row_drawer_8__16), .col7(row_drawer_8__17));
  video_handler video_handler_1 (
    .row_num(processor_hadnler_1_row_num), .clk(processor_hadnler_1_st_row_out), .left_clk(left_row),
    .right_clk(right_row), .clk_0(_0_clk), .clk_1(_1_clk), .clk_2(_2_clk), .clk_3(_3_clk), .clk_4(_4_clk),
    .clk_5(_5_clk), .clk_6(_6_clk), .clk_7(_7_clk), .selected(processor_hadnler_1_selected),
    .clk_0_2(selected_0), .clk_1_2(selected_1), .clk_2_2(selected_2), .clk_3_2(selected_3),
    .clk_4_2(selected_4), .clk_5_2(selected_5), .clk_6_2(selected_6), .clk_7_2(selected_7),
    .selected_col(selected_cell));
  DotMatrix #(.matrixcols(8)) dotmatrix_18 (
    .col0(row_drawer_1__20), .col1(row_drawer_1__21), .col2(row_drawer_1__22), .col3(row_drawer_1__23),
    .col4(row_drawer_1__24), .col5(row_drawer_1__25), .col6(row_drawer_1__26), .col7(row_drawer_1__27));
  DotMatrix #(.matrixcols(8)) dotmatrix_19 (
    .col0(row_drawer_2__20), .col1(row_drawer_2__21), .col2(row_drawer_2__22), .col3(row_drawer_2__23),
    .col4(row_drawer_2__24), .col5(row_drawer_2__25), .col6(row_drawer_2__26), .col7(row_drawer_2__27));
  DotMatrix #(.matrixcols(8)) dotmatrix_20 (
    .col0(row_drawer_3__20), .col1(row_drawer_3__21), .col2(row_drawer_3__22), .col3(row_drawer_3__23),
    .col4(row_drawer_3__24), .col5(row_drawer_3__25), .col6(row_drawer_3__26), .col7(row_drawer_3__27));
  DotMatrix #(.matrixcols(8)) dotmatrix_21 (
    .col0(row_drawer_4__20), .col1(row_drawer_4__21), .col2(row_drawer_4__22), .col3(row_drawer_4__23),
    .col4(row_drawer_4__24), .col5(row_drawer_4__25), .col6(row_drawer_4__26), .col7(row_drawer_4__27));
  DotMatrix #(.matrixcols(8)) dotmatrix_22 (
    .col0(row_drawer_5__20), .col1(row_drawer_5__21), .col2(row_drawer_5__22), .col3(row_drawer_5__23),
    .col4(row_drawer_5__24), .col5(row_drawer_5__25), .col6(row_drawer_5__26), .col7(row_drawer_5__27));
  DotMatrix #(.matrixcols(8)) dotmatrix_23 (
    .col0(row_drawer_6__20), .col1(row_drawer_6__21), .col2(row_drawer_6__22), .col3(row_drawer_6__23),
    .col4(row_drawer_6__24), .col5(row_drawer_6__25), .col6(row_drawer_6__26), .col7(row_drawer_6__27));
  DotMatrix #(.matrixcols(8)) dotmatrix_24 (
    .col0(row_drawer_7__20), .col1(row_drawer_7__21), .col2(row_drawer_7__22), .col3(row_drawer_7__23),
    .col4(row_drawer_7__24), .col5(row_drawer_7__25), .col6(row_drawer_7__26), .col7(row_drawer_7__27));
  DotMatrix #(.matrixcols(8)) dotmatrix_25 (
    .col0(row_drawer_8__20), .col1(row_drawer_8__21), .col2(row_drawer_8__22), .col3(row_drawer_8__23),
    .col4(row_drawer_8__24), .col5(row_drawer_8__25), .col6(row_drawer_8__26), .col7(row_drawer_8__27));
  DotMatrix #(.matrixcols(8)) dotmatrix_26 (
    .col0(row_drawer_1__30), .col1(row_drawer_1__31), .col2(row_drawer_1__32), .col3(row_drawer_1__33),
    .col4(row_drawer_1__34), .col5(row_drawer_1__35), .col6(row_drawer_1__36), .col7(row_drawer_1__37));
  DotMatrix #(.matrixcols(8)) dotmatrix_27 (
    .col0(row_drawer_2__30), .col1(row_drawer_2__31), .col2(row_drawer_2__32), .col3(row_drawer_2__33),
    .col4(row_drawer_2__34), .col5(row_drawer_2__35), .col6(row_drawer_2__36), .col7(row_drawer_2__37));
  DotMatrix #(.matrixcols(8)) dotmatrix_28 (
    .col0(row_drawer_3__30), .col1(row_drawer_3__31), .col2(row_drawer_3__32), .col3(row_drawer_3__33),
    .col4(row_drawer_3__34), .col5(row_drawer_3__35), .col6(row_drawer_3__36), .col7(row_drawer_3__37));
  DotMatrix #(.matrixcols(8)) dotmatrix_29 (
    .col0(row_drawer_4__30), .col1(row_drawer_4__31), .col2(row_drawer_4__32), .col3(row_drawer_4__33),
    .col4(row_drawer_4__34), .col5(row_drawer_4__35), .col6(row_drawer_4__36), .col7(row_drawer_4__37));
  DotMatrix #(.matrixcols(8)) dotmatrix_30 (
    .col0(row_drawer_5__30), .col1(row_drawer_5__31), .col2(row_drawer_5__32), .col3(row_drawer_5__33),
    .col4(row_drawer_5__34), .col5(row_drawer_5__35), .col6(row_drawer_5__36), .col7(row_drawer_5__37));
  DotMatrix #(.matrixcols(8)) dotmatrix_31 (
    .col0(row_drawer_6__30), .col1(row_drawer_6__31), .col2(row_drawer_6__32), .col3(row_drawer_6__33),
    .col4(row_drawer_6__34), .col5(row_drawer_6__35), .col6(row_drawer_6__36), .col7(row_drawer_6__37));
  DotMatrix #(.matrixcols(8)) dotmatrix_32 (
    .col0(row_drawer_7__30), .col1(row_drawer_7__31), .col2(row_drawer_7__32), .col3(row_drawer_7__33),
    .col4(row_drawer_7__34), .col5(row_drawer_7__35), .col6(row_drawer_7__36), .col7(row_drawer_7__37));
  DotMatrix #(.matrixcols(8)) dotmatrix_33 (
    .col0(row_drawer_8__30), .col1(row_drawer_8__31), .col2(row_drawer_8__32), .col3(row_drawer_8__33),
    .col4(row_drawer_8__34), .col5(row_drawer_8__35), .col6(row_drawer_8__36), .col7(row_drawer_8__37));
  DotMatrix #(.matrixcols(8)) dotmatrix_34 (
    .col0(row_drawer_1__40), .col1(row_drawer_1__41), .col2(row_drawer_1__42), .col3(row_drawer_1__43),
    .col4(row_drawer_1__44), .col5(row_drawer_1__45), .col6(row_drawer_1__46), .col7(row_drawer_1__47));
  DotMatrix #(.matrixcols(8)) dotmatrix_35 (
    .col0(row_drawer_2__40), .col1(row_drawer_2__41), .col2(row_drawer_2__42), .col3(row_drawer_2__43),
    .col4(row_drawer_2__44), .col5(row_drawer_2__45), .col6(row_drawer_2__46), .col7(row_drawer_2__47));
  DotMatrix #(.matrixcols(8)) dotmatrix_36 (
    .col0(row_drawer_3__40), .col1(row_drawer_3__41), .col2(row_drawer_3__42), .col3(row_drawer_3__43),
    .col4(row_drawer_3__44), .col5(row_drawer_3__45), .col6(row_drawer_3__46), .col7(row_drawer_3__47));
  DotMatrix #(.matrixcols(8)) dotmatrix_37 (
    .col0(row_drawer_4__40), .col1(row_drawer_4__41), .col2(row_drawer_4__42), .col3(row_drawer_4__43),
    .col4(row_drawer_4__44), .col5(row_drawer_4__45), .col6(row_drawer_4__46), .col7(row_drawer_4__47));
  DotMatrix #(.matrixcols(8)) dotmatrix_38 (
    .col0(row_drawer_5__40), .col1(row_drawer_5__41), .col2(row_drawer_5__42), .col3(row_drawer_5__43),
    .col4(row_drawer_5__44), .col5(row_drawer_5__45), .col6(row_drawer_5__46), .col7(row_drawer_5__47));
  DotMatrix #(.matrixcols(8)) dotmatrix_39 (
    .col0(row_drawer_6__40), .col1(row_drawer_6__41), .col2(row_drawer_6__42), .col3(row_drawer_6__43),
    .col4(row_drawer_6__44), .col5(row_drawer_6__45), .col6(row_drawer_6__46), .col7(row_drawer_6__47));
  DotMatrix #(.matrixcols(8)) dotmatrix_40 (
    .col0(row_drawer_7__40), .col1(row_drawer_7__41), .col2(row_drawer_7__42), .col3(row_drawer_7__43),
    .col4(row_drawer_7__44), .col5(row_drawer_7__45), .col6(row_drawer_7__46), .col7(row_drawer_7__47));
  DotMatrix #(.matrixcols(8)) dotmatrix_41 (
    .col0(row_drawer_8__40), .col1(row_drawer_8__41), .col2(row_drawer_8__42), .col3(row_drawer_8__43),
    .col4(row_drawer_8__44), .col5(row_drawer_8__45), .col6(row_drawer_8__46), .col7(row_drawer_8__47));
  DotMatrix #(.matrixcols(8), .matrixrows(14)) dotmatrix_42 (
    .col0(info_display_1__00_4), .col1(info_display_1__01_4), .col2(info_display_1__00_9),
    .col3(info_display_1__01_9), .col4(info_display_1__00_14), .col5(info_display_1__01_14),
    .col6(info_display_1__00_19), .col7(info_display_1__01_19));
  DotMatrix #(.matrixcols(8)) dotmatrix_43 (
    .col0(row_drawer_1__50), .col1(row_drawer_1__51), .col2(row_drawer_1__52), .col3(row_drawer_1__53),
    .col4(row_drawer_1__54), .col5(row_drawer_1__55), .col6(row_drawer_1__56), .col7(row_drawer_1__57));
  DotMatrix #(.matrixcols(8)) dotmatrix_44 (
    .col0(row_drawer_2__50), .col1(row_drawer_2__51), .col2(row_drawer_2__52), .col3(row_drawer_2__53),
    .col4(row_drawer_2__54), .col5(row_drawer_2__55), .col6(row_drawer_2__56), .col7(row_drawer_2__57));
  DotMatrix #(.matrixcols(8)) dotmatrix_45 (
    .col0(row_drawer_3__50), .col1(row_drawer_3__51), .col2(row_drawer_3__52), .col3(row_drawer_3__53),
    .col4(row_drawer_3__54), .col5(row_drawer_3__55), .col6(row_drawer_3__56), .col7(row_drawer_3__57));
  DotMatrix #(.matrixcols(8)) dotmatrix_46 (
    .col0(row_drawer_4__50), .col1(row_drawer_4__51), .col2(row_drawer_4__52), .col3(row_drawer_4__53),
    .col4(row_drawer_4__54), .col5(row_drawer_4__55), .col6(row_drawer_4__56), .col7(row_drawer_4__57));
  DotMatrix #(.matrixcols(8)) dotmatrix_47 (
    .col0(row_drawer_5__50), .col1(row_drawer_5__51), .col2(row_drawer_5__52), .col3(row_drawer_5__53),
    .col4(row_drawer_5__54), .col5(row_drawer_5__55), .col6(row_drawer_5__56), .col7(row_drawer_5__57));
  DotMatrix #(.matrixcols(8)) dotmatrix_48 (
    .col0(row_drawer_6__50), .col1(row_drawer_6__51), .col2(row_drawer_6__52), .col3(row_drawer_6__53),
    .col4(row_drawer_6__54), .col5(row_drawer_6__55), .col6(row_drawer_6__56), .col7(row_drawer_6__57));
  DotMatrix #(.matrixcols(8)) dotmatrix_49 (
    .col0(row_drawer_7__50), .col1(row_drawer_7__51), .col2(row_drawer_7__52), .col3(row_drawer_7__53),
    .col4(row_drawer_7__54), .col5(row_drawer_7__55), .col6(row_drawer_7__56), .col7(row_drawer_7__57));
  DotMatrix #(.matrixcols(8)) dotmatrix_50 (
    .col0(row_drawer_8__50), .col1(row_drawer_8__51), .col2(row_drawer_8__52), .col3(row_drawer_8__53),
    .col4(row_drawer_8__54), .col5(row_drawer_8__55), .col6(row_drawer_8__56), .col7(row_drawer_8__57));
  DotMatrix #(.matrixcols(8)) dotmatrix_51 (
    .col0(row_drawer_1__60), .col1(row_drawer_1__61), .col2(row_drawer_1__62), .col3(row_drawer_1__63),
    .col4(row_drawer_1__64), .col5(row_drawer_1__65), .col6(row_drawer_1__66), .col7(row_drawer_1__67));
  DotMatrix #(.matrixcols(8)) dotmatrix_52 (
    .col0(row_drawer_2__60), .col1(row_drawer_2__61), .col2(row_drawer_2__62), .col3(row_drawer_2__63),
    .col4(row_drawer_2__64), .col5(row_drawer_2__65), .col6(row_drawer_2__66), .col7(row_drawer_2__67));
  DotMatrix #(.matrixcols(8)) dotmatrix_53 (
    .col0(row_drawer_3__60), .col1(row_drawer_3__61), .col2(row_drawer_3__62), .col3(row_drawer_3__63),
    .col4(row_drawer_3__64), .col5(row_drawer_3__65), .col6(row_drawer_3__66), .col7(row_drawer_3__67));
  DotMatrix #(.matrixcols(8)) dotmatrix_54 (
    .col0(row_drawer_4__60), .col1(row_drawer_4__61), .col2(row_drawer_4__62), .col3(row_drawer_4__63),
    .col4(row_drawer_4__64), .col5(row_drawer_4__65), .col6(row_drawer_4__66), .col7(row_drawer_4__67));
  DotMatrix #(.matrixcols(8)) dotmatrix_55 (
    .col0(row_drawer_5__60), .col1(row_drawer_5__61), .col2(row_drawer_5__62), .col3(row_drawer_5__63),
    .col4(row_drawer_5__64), .col5(row_drawer_5__65), .col6(row_drawer_5__66), .col7(row_drawer_5__67));
  DotMatrix #(.matrixcols(8)) dotmatrix_56 (
    .col0(row_drawer_6__60), .col1(row_drawer_6__61), .col2(row_drawer_6__62), .col3(row_drawer_6__63),
    .col4(row_drawer_6__64), .col5(row_drawer_6__65), .col6(row_drawer_6__66), .col7(row_drawer_6__67));
  DotMatrix #(.matrixcols(8)) dotmatrix_57 (
    .col0(row_drawer_7__60), .col1(row_drawer_7__61), .col2(row_drawer_7__62), .col3(row_drawer_7__63),
    .col4(row_drawer_7__64), .col5(row_drawer_7__65), .col6(row_drawer_7__66), .col7(row_drawer_7__67));
  DotMatrix #(.matrixcols(8)) dotmatrix_58 (
    .col0(row_drawer_8__60), .col1(row_drawer_8__61), .col2(row_drawer_8__62), .col3(row_drawer_8__63),
    .col4(row_drawer_8__64), .col5(row_drawer_8__65), .col6(row_drawer_8__66), .col7(row_drawer_8__67));
  DotMatrix #(.matrixcols(8)) dotmatrix_59 (
    .col0(row_drawer_1__70), .col1(row_drawer_1__71), .col2(row_drawer_1__72), .col3(row_drawer_1__73),
    .col4(row_drawer_1__74), .col5(row_drawer_1__75), .col6(row_drawer_1__76), .col7(row_drawer_1__77));
  DotMatrix #(.matrixcols(8)) dotmatrix_60 (
    .col0(row_drawer_2__70), .col1(row_drawer_2__71), .col2(row_drawer_2__72), .col3(row_drawer_2__73),
    .col4(row_drawer_2__74), .col5(row_drawer_2__75), .col6(row_drawer_2__76), .col7(row_drawer_2__77));
  DotMatrix #(.matrixcols(8)) dotmatrix_61 (
    .col0(row_drawer_3__70), .col1(row_drawer_3__71), .col2(row_drawer_3__72), .col3(row_drawer_3__73),
    .col4(row_drawer_3__74), .col5(row_drawer_3__75), .col6(row_drawer_3__76), .col7(row_drawer_3__77));
  DotMatrix #(.matrixcols(8)) dotmatrix_62 (
    .col0(row_drawer_4__70), .col1(row_drawer_4__71), .col2(row_drawer_4__72), .col3(row_drawer_4__73),
    .col4(row_drawer_4__74), .col5(row_drawer_4__75), .col6(row_drawer_4__76), .col7(row_drawer_4__77));
  DotMatrix #(.matrixcols(8)) dotmatrix_63 (
    .col0(row_drawer_5__70), .col1(row_drawer_5__71), .col2(row_drawer_5__72), .col3(row_drawer_5__73),
    .col4(row_drawer_5__74), .col5(row_drawer_5__75), .col6(row_drawer_5__76), .col7(row_drawer_5__77));
  DotMatrix #(.matrixcols(8)) dotmatrix_64 (
    .col0(row_drawer_6__70), .col1(row_drawer_6__71), .col2(row_drawer_6__72), .col3(row_drawer_6__73),
    .col4(row_drawer_6__74), .col5(row_drawer_6__75), .col6(row_drawer_6__76), .col7(row_drawer_6__77));
  DotMatrix #(.matrixcols(8)) dotmatrix_65 (
    .col0(row_drawer_7__70), .col1(row_drawer_7__71), .col2(row_drawer_7__72), .col3(row_drawer_7__73),
    .col4(row_drawer_7__74), .col5(row_drawer_7__75), .col6(row_drawer_7__76), .col7(row_drawer_7__77));
  DotMatrix #(.matrixcols(8)) dotmatrix_66 (
    .col0(row_drawer_8__70), .col1(row_drawer_8__71), .col2(row_drawer_8__72), .col3(row_drawer_8__73),
    .col4(row_drawer_8__74), .col5(row_drawer_8__75), .col6(row_drawer_8__76), .col7(row_drawer_8__77));
  assign or_1_out = f_out_0 | f_out_2;  // OR_Gate or_1, 8 bits wide
  assign or_2_out = f_out_1 | f_out_3;  // OR_Gate or_2, 8 bits wide
  assign or_3_out = f_out_2 | f_out_4;  // OR_Gate or_3, 8 bits wide
  assign or_4_out = f_out_3 | f_out_5;  // OR_Gate or_4, 8 bits wide
  assign or_5_out = f_out_4 | f_out_6;  // OR_Gate or_5, 8 bits wide
  assign or_6_out = f_out_5 | f_out_7;  // OR_Gate or_6, 8 bits wide
endmodule

module processor_hadnler (
  input  clk,
  input  IRQ,
  input  reset,
  input  start,
  input  [2:0] vec,
  output Ack,
  output st_row_out,
  output flag,
  output [3:0] row_num,
  output open,
  output [31:0] row_out,
  output win,
  output [7:0] selected,
  output lose,
  output [7:0] flags
);

  wire and_1_out, and_3_out, and_4_out, and_5_out, and_6_out, and_7_out, and_8_out, and_9_out, and_10_out,
       button_1_out, button_2_out, button_3_out, cdm_8_mark5_1_data_inst, cdm_8_mark5_1_mem_cycle,
       cell_0_upd, cell_1_upd, cell_2_upd, cell_3_upd, clk_t, clk_t_t, clock_1_out, comparator_3_eq,
       comparator_4_eq, comparator_5_eq, comparator_6_lt, comparator_7_eq, comparator_8_eq, d_ff_1_q,
       decoder_2_out0, decoder_2_out1, decoder_2_out2, decoder_2_out3, IRQ_t, map_loaded, map_sel,
       multiplexer_2_out, multiplexer_3_out, nor_1_out, not_1_out, not_2_out, not_3_out, not_4_out,
       not_5_out, not_6_out, or_1_out, or_4_out, or_5_out, program_sel, reset_t, t_ff_1_q, t_ff_2_q, wr;
  wire [2:0] controlled_buffer_1_out;
  wire [7:0] addr, cdm_8_mark5_1_data_out, cdm_8_mark5_1_ps, cdm_8_mark5_1_r0, cdm_8_mark5_1_r1,
       cdm_8_mark5_1_r2, cdm_8_mark5_1_r3, cdm_8_mark5_1_sp, controlled_buffer_2_out, counter_2_q, data,
       map_loader_1_data, map_loader_addr, map_loader_addr_ROM, map_offsest, multiplexer_1_out,
       multiplexer_4_out, pc, ram_1_data;

  Clock clock_1 (.out(clock_1_out));
  Button button_1 (.out(button_1_out));
  Button button_2 (.out(button_2_out));
  Button button_3 (.out(button_3_out));
  or or_1 (or_1_out, clock_1_out, clk);
  or or_2 (IRQ_t, button_1_out, IRQ);
  or or_3 (reset_t, button_2_out, reset);
  or or_4 (or_4_out, button_3_out, start);
  // Probe on vec
  D_Flip_Flop d_ff_1 (.clk(reset_t), .D(1'b1), .Q(d_ff_1_q), .reset(or_4_out));  // open: Qn, preset, en
  // Probe on cdm_8_mark5_1_r3
  // Probe on cdm_8_mark5_1_r2
  // Probe on pc
  // Probe on cdm_8_mark5_1_r1
  // Probe on cdm_8_mark5_1_r0
  assign controlled_buffer_1_out = Ack ? vec : 3'bz;  // Controlled_Buffer controlled_buffer_1
  and and_1 (and_1_out, clk_t, map_loaded);
  and and_2 (clk_t, or_1_out, ~d_ff_1_q);  // AND_Gate
  // Probe on cdm_8_mark5_1_sp
  // Probe on cdm_8_mark5_1_ps
  Decoder #(.disabled(0)) decoder_1 (
    .out0(program_sel), .out1(map_sel), .sel(cdm_8_mark5_1_data_inst), .en(cdm_8_mark5_1_mem_cycle));
  CdM_8_mark5 cdm_8_mark5_1 (
    .clock(and_1_out), .addr(addr), .mem_read(wr), .mem_cycle(cdm_8_mark5_1_mem_cycle),
    .data_inst(cdm_8_mark5_1_data_inst), .data_out(cdm_8_mark5_1_data_out),
    .data_in(controlled_buffer_2_out), .r0(cdm_8_mark5_1_r0), .r1(cdm_8_mark5_1_r1), .r2(cdm_8_mark5_1_r2),
    .r3(cdm_8_mark5_1_r3), .PC(pc), .SP(cdm_8_mark5_1_sp), .PS(cdm_8_mark5_1_ps), .IAck(Ack), .IRQ(IRQ_t),
    .vec(controlled_buffer_1_out));
  assign controlled_buffer_2_out = wr ? data : 8'bz;  // Controlled_Buffer controlled_buffer_2
  Pull_Resistor pull_resistor_1 (.node(vec));
  not not_1 (not_1_out, wr);
  assign data = not_1_out ? cdm_8_mark5_1_data_out : 8'bz;  // Controlled_Buffer controlled_buffer_3
  Comparator comparator_1 (.a(pc), .b(8'ha4), .eq(flag));  // open: gt, lt
  Comparator #(.width(3)) comparator_2 (.a(vec), .b(3'b100), .eq(open));  // open: gt, lt
  Comparator comparator_3 (.a(pc), .b(8'hdf), .eq(comparator_3_eq));  // open: gt, lt
  Comparator comparator_4 (.a(pc), .b(8'he1), .eq(comparator_4_eq));  // open: gt, lt
  Counter counter_1 (.Q(map_loader_addr), .clk(cell_0_upd), .clr(reset_t));  // open: load, D, count, carry
  D_Flip_Flop d_ff_2 (.clk(comparator_3_eq), .D(1'b1), .Q(win), .reset(reset_t));  // open: Qn, preset, en
  D_Flip_Flop d_ff_3 (.clk(comparator_4_eq), .D(1'b1), .Q(lose), .reset(reset_t));  // open: Qn, preset, en
  Adder adder_1 (.a(8'h4), .b(map_loader_addr), .out(map_loader_addr_ROM));  // open: cin, cout
  // Probe on addr
  and and_3 (and_3_out, program_sel, map_loaded);
  ROM rom_1 (.addr(addr), .data(data), .sel(and_3_out));
  // Probe on data
  and and_4 (and_4_out, t_ff_2_q, ~t_ff_1_q);  // AND_Gate
  Comparator comparator_5 (.a(map_loader_addr_ROM), .b(8'h4), .eq(comparator_5_eq));  // open: gt, lt
  and and_5 (and_5_out, clk_t_t, ~st_row_out);  // AND_Gate
  map_loader map_loader_1 (
    .clk(and_5_out), .reset(reset_t), .loaded(map_loaded), .data(map_loader_1_data), .addr(map_offsest));
  and and_6 (and_6_out, clk_t_t, ~map_loaded);  // AND_Gate
  or or_5 (or_5_out, and_6_out, and_4_out);
  T_Flip_Flop t_ff_1 (.clk(and_4_out), .T(and_4_out), .Q(t_ff_1_q), .reset(not_2_out));  // open: Qn, preset, en
  not not_2 (not_2_out, reset_t);
  Multiplexer #(.width(8), .disabled(0), .enable("false")) multiplexer_1 (
    .in0(map_loader_addr_ROM), .in1(addr), .out(multiplexer_1_out), .sel(map_loaded));
  // Probe on multiplexer_1_out
  nor nor_1 (nor_1_out, map_loaded, comparator_5_eq);
  Multiplexer #(.enable("false")) multiplexer_2 (
    .in0(nor_1_out), .in1(map_sel), .out(multiplexer_2_out), .sel(map_loaded));
  // Probe on map_loader_1_data
  Counter #(.max('h4), .trigger("falling")) counter_2 (
    .load(reset_t), .D(8'h4), .Q(counter_2_q), .clk(or_5_out), .clr(and_7_out));  // open: count, carry
  Comparator comparator_6 (.a(counter_2_q), .b(8'h4), .eq(st_row_out), .lt(comparator_6_lt));  // open: gt
  T_Flip_Flop t_ff_2 (.clk(and_7_out), .T(and_7_out), .Q(t_ff_2_q), .reset(not_3_out));  // open: Qn, preset, en
  not not_3 (not_3_out, reset_t);
  and and_7 (and_7_out, reset_t, ~t_ff_2_q);  // AND_Gate
  and and_8 (and_8_out, map_loaded, wr);
  Multiplexer #(.disabled(0), .enable("false")) multiplexer_3 (
    .in0(st_row_out), .in1(not_4_out), .out(multiplexer_3_out), .sel(map_loaded));
  not not_4 (not_4_out, clk_t);
  not not_5 (not_5_out, map_loaded);
  Decoder #(.select(3), .disabled(0)) decoder_2 (
    .out0(decoder_2_out0), .out1(decoder_2_out1), .out2(decoder_2_out2), .out3(decoder_2_out3),
    .sel(counter_2_q[2:0]), .en(comparator_6_lt));  // open: out4, out5, out6, out7
  // Probe on counter_2_q[2:0]
  // Probe on data
  RAM ram_1 (
    .addr(multiplexer_1_out), .data(ram_1_data), .sel(multiplexer_2_out), .clk(multiplexer_3_out),
    .ld(and_8_out));  // open: clr
  assign data = and_8_out ? ram_1_data : 8'bz;  // Controlled_Buffer controlled_buffer_4
  // Probe on ram_1_data
  assign ram_1_data = not_6_out ? multiplexer_4_out : 8'bz;  // Controlled_Buffer controlled_buffer_5
  // Probe on ram_1_data
  not not_6 (not_6_out, and_8_out);
  Register register_1 (.D(map_loader_1_data), .en(not_5_out), .Q(row_out[7:0]), .clk(decoder_2_out0), .clr(reset_t));
  delayer delayer_1 (.bus_0(decoder_2_out0), .second(cell_0_upd));  // open: first
  Multiplexer #(.width(8), .enable("false")) multiplexer_4 (
    .in0({1'b0, row_out[3], 1'b0, row_out[11], 1'b0, row_out[19], 1'b0, row_out[27]}), .in1(data),
    .out(multiplexer_4_out), .sel(map_loaded));
  Register register_2 (.D(map_loader_1_data), .en(not_5_out), .Q(row_out[23:16]), .clk(decoder_2_out2), .clr(reset_t));
  Register register_3 (.D(map_loader_1_data), .en(not_5_out), .Q(row_out[15:8]), .clk(decoder_2_out1), .clr(reset_t));
  delayer delayer_2 (.bus_0(decoder_2_out2), .second(cell_2_upd));  // open: first
  delayer delayer_3 (.bus_0(decoder_2_out1), .second(cell_1_upd));  // open: first
  and and_9 (and_9_out, ~wr, map_sel, comparator_7_eq);  // AND_Gate
  Comparator comparator_7 (.a(addr), .b(8'h2), .eq(comparator_7_eq));  // open: gt, lt
  and and_10 (and_10_out, ~wr, map_sel, comparator_8_eq);  // AND_Gate
  Comparator comparator_8 (.a(addr), .b(8'h4), .eq(comparator_8_eq));  // open: gt, lt
  Register register_4 (.D(map_loader_1_data), .en(not_5_out), .Q(row_out[31:24]), .clk(decoder_2_out3), .clr(reset_t));
  delayer delayer_4 (.bus_0(decoder_2_out3), .second(cell_3_upd));  // open: first
  Subtractor #(.width(4)) subtractor_1 (.a(map_loader_addr[3:0]), .b(4'b0001), .out(row_num));  // open: bin, bout
  Register register_5 (.D(data), .en(and_9_out), .Q(selected), .clk(clk_t), .clr(reset_t));
  Register register_6 (.D(data), .en(and_10_out), .Q(flags), .clk(clk_t), .clr(reset_t));

  // Other names for the same wires on the sheet: IAck = Ack; map_register_full = st_row_out;
  //   cell_0[7:0] = row_out[7:0]; mapped_cell (some bits) = {row_out[3], row_out[11], row_out[19], row_out[27]};
  //   cell_1[7:0] = row_out[15:8]; cell_2[7:0] = row_out[23:16]; cell_3[7:0] = row_out[31:24]

  // Notes on the sheet:
  //   program
  //   Memory
  //   Map loader
  //   contents of rom_1 (hex, n*v repeats v):
  //   ee 6 4*0 cd f0 c1 d1 10 c1 d1 80 c1 d9 c5 d6 cd d5 ee 13 d2 2 b8 d1 7 41 e1 23 d1 7 14 ee 24 88 a8
  //   d9 d2 2 b8 d1 7 bb 8f 47 e1 34 85 14 ee 35 8c a8 d9 d2 2 b8 d1 8 71 ea 44 d1 38 14 ee 48 d1 8 31 4
  //   a8 d9 d2 2 b8 d1 38 71 eb 58 d1 38 31 4 ee 5b d1 8 14 a8 d9 d2 2 b9 c1 99 99 d2 5 16 b8 c5 d7 d0 3
  //   d2 80 d3 40 44 0 e0 7a 93 93 92 92 88 ee 70 d7 d6 5d c0 d6 69 c4 42 e0 85 d9 43 e0 8a ee e1 d9 d6 5d
  //   c2 c0 d6 69 d1 4 b5 5 e1 9f c4 c0 48 e1 9f c4 c4 d9 c4 68 c5 a4 42 e1 b3 d1 1 43 e0 af d2 1 ee b1 d2
  //   0 ee be d1 ff 43 e0 bc d2 ff ee be d2 0 d3 3 bc 18 0 e1 c7 ee df ac 8f bc 14 ac d9 d0 3 d1 a a1 8c
  //   a1 d7 d6 cd d0 2 d1 0 a1 d9 d1 0 ee 6 ee 6 13*0 16 0 26 0 37 0 4a 0 7b 0 8b 0 d5
  //   map
endmodule

module map_selector (
  input  [7:0] addr,
  input  sel,
  input  clk,
  output [7:0] cell_info
);

  wire decoder_1_out0, decoder_1_out1, decoder_1_out2, decoder_1_out3, decoder_1_out4, decoder_1_out5,
       decoder_1_out6, decoder_1_out7;
  wire [1:0] offset;
  wire [5:0] seed;
  wire [7:0] addr_t, multiplier_1_out;

  Decoder #(.select(3), .enable("false")) decoder_1 (
    .out0(decoder_1_out0), .out1(decoder_1_out1), .out2(decoder_1_out2), .out3(decoder_1_out3),
    .out4(decoder_1_out4), .out5(decoder_1_out5), .out6(decoder_1_out6), .out7(decoder_1_out7),
    .sel({seed[1:0], seed[2]}));
  ROM rom_1 (.addr(addr_t), .data(cell_info), .sel(decoder_1_out0));
  ROM rom_2 (.addr(addr_t), .data(cell_info), .sel(decoder_1_out2));
  ROM rom_3 (.addr(addr_t), .data(cell_info), .sel(decoder_1_out4));
  ROM rom_4 (.addr(addr_t), .data(cell_info), .sel(decoder_1_out6));
  ROM rom_5 (.addr(addr_t), .data(cell_info), .sel(decoder_1_out1));
  ROM rom_6 (.addr(addr_t), .data(cell_info), .sel(decoder_1_out3));
  ROM rom_7 (.addr(addr_t), .data(cell_info), .sel(decoder_1_out5));
  ROM rom_8 (.addr(addr_t), .data(cell_info), .sel(decoder_1_out7));
  // Probe on {{6{1'b0}}, offset}
  Multiplier multiplier_1 (.a({{6{1'b0}}, offset}), .b(8'h40), .out(multiplier_1_out));  // open: cin, cout
  Adder adder_1 (.a(addr), .b(multiplier_1_out), .out(addr_t));  // open: cin, cout
  Random random_1 (.clk(clk), .out({offset, seed}));  // open: next, clr

  // Other names for the same wires on the sheet: seed[7:6] = offset; row_addr[7:0] = addr

  // Notes on the sheet:
  //   contents of rom_1 (hex, n*v repeats v):
  //   1 8 1 0 0 6*1 0 1 2 8 1 4*0 2 8 3 1 4*0 2 8 2 0 1 1 0 0 2 2 3 1 8 1 0 0 1 8 4 8 1 1 0 0 1 3 8 8 5*0
  //   2 8 3 4*0 2 8 2 5*0 2 8 2 0 1 1 1 0 1 2 2 1 1 8 1 0 0 2 8 2 1 1 2 2 2 3 8 3 1 1 2 8 8 2 2 8 2 8 3 2
  //   2 1 1 1 2 8 2 5*0 1 2 8 1 1 8 2 8 1 8 2 1 1 2 3 2 1 1 1 0 0 1 8 1 5*0 1 2 2 6*0 1 8 0 0 1 1 1 0 1 1
  //   0 0 1 8 3 2 2 1 0 0 1 2 8 8 2 8 0 1 1 1 0 1 8 1 0 2 8 2 0 1 1 1 0 2 8 2 1 2 2 1 0 4*1 8 8 2 0 0 1 1
  //   2 4 8 4 0 0 1 8 1 2 8 8 0 0 1 1 2 2 3 2 4*0 1 8 1
  //   contents of rom_2 (hex, n*v repeats v):
  //   8 8 1 1 8 8 1 0 2 2 1 1 2 2 1 12*0 1 1 1 0 0 1 1 1 3 8 3 1 1 8 2 1 8 8 3 8 1 8 2 1 2 2 2 4*1 7*0 1 1
  //   1 0 0 1 1 1 2 8 1 0 0 1 8 8 3 2 2 0 0 1 1 2 3 8 1 0 0 1 1 8 3 1 1 0 1 2 8 8 2 0 1 1 2 8 2 1 1 0 1 8
  //   2 2 2 0 0 0 4*1 8 1 3 8 2 4*0 2 8 8 3 4*0 3 8 8 2 4*0 2 8 3 1 0 1 1 1 2 2 2 0 0 1 8 1 1 8 1 1 1 2 1
  //   1 2 2 1 1 8 1 0 0 8 1 0 1 1 1 0 0 1 8 1 5*0 1 1 1 7*0 4*1 2 2 0 0 1 8 2 2 8 8 0 0 1 2 8 2 2 2 1 1 2
  //   2 2 4*1 8 2 8 2 1 2 8 1 1 2 2 8 1 2 8
  //   contents of rom_3 (hex, n*v repeats v):
  //   4*0 1 1 2 8 1 1 1 0 1 8 2 1 1 8 1 0 1 1 1 0 1 2 3 2 5*1 2 8 8 1 1 8 2 1 8 3 2 1 1 3 8 1 1 1 0 0 0 3
  //   8 6*0 2 8 1 8 1 5*0 1 1 2 2 2 1 4*0 1 8 8 1 0 0 1 1 4*2 1 1 2 8 2 1 0 1 8 1 8 4 8 1 0 1 1 1 2 8 4 3
  //   1 0 0 0 1 2 8 8 1 0 0 0 1 2 8 1 0 0 1 8 8 3 4*2 3 2 8 2 1 8 2 8 8 1 1 6*2 1 0 1 8 2 1 4*0 1 2 8 1
  //   5*0 1 1 2 1 1 5*0 1 8 1 9*0 1 1 1 5*0 2 8 2 0 1 1 1 0 3 8 4 1 2 8 1 0 3 8 4 8 2 2 3 2 2 8 4 2 1 1 8
  //   8 1 2 8 1 1 2 3 2 0 4*1 8 1
  //   contents of rom_4 (hex, n*v repeats v):
  //   0 0 0 2 8 2 1 1 2 3 2 3 8 2 1 4*8 2 4*1 3 8 3 1 0 1 1 1 2 3 3 1 0 1 8 1 1 8 8 1 0 4*1 2 2 1 18*0 1 8
  //   1 1 2 1 2 1 2 1 2 8 3 8 3 8 1 0 8 2 4 8 5 2 2 0 1 1 3 8 4 8 1 0 0 0 3 8 4 1 1 0 0 0 2 8 2 5*0 1 1 1
  //   5*0 1 8 2 8 1 0 0 0 1 1 2 1 1 5*0 1 1 1 0 1 1 1 2 3 8 2 1 8 1 1 8 8 2 2 8 4*2 3 2 2 1 1 8 1 1 2 8 1
  //   0 4*1 8 2 1 0 8 2 1 5*0 2 8 1 0 0 0 5*1 0 0 0 1 8 1 1 1 0 0 0 1 1 2 8 2 0 1 1 2 1 2 8 2 0 1 8 3 8 1
  //   1 2 1 2 3 8 3 0 0 1 8 1 2 8 2
  //   contents of rom_5 (hex, n*v repeats v):
  //   0 1 8 1 4*0 1 3 3 3 2 2 1 0 1 8 8 2 8 8 1 0 1 5*2 1 0 8*1 8 2 2 8 1 1 8 1 2 8 3 2 5*1 2 8 1 4*0 1 1
  //   6*0 8 2 5*1 0 1 2 8 1 1 8 2 1 0 2 3 3 2 2 8 1 0 1 8 8 2 1 1 1 0 1 3 8 2 0 0 0 1 2 2 3 2 1 0 0 8 2 8
  //   2 8 1 0 0 1 1 2 1 1 0 0 0 2 8 3 8 2 1 0 0 2 8 3 3 8 2 0 0 1 1 1 2 8 2 0 0 2 2 4*1 0 0 8 8 2 1 4*0 2
  //   3 8 2 4*1 0 1 1 2 8 1 1 8 0 0 1 2 8 1 4*0 2 8 3 1 0 0 1 1 4 8 3 4*1 8 3 8 2 2 8 2 1 2 3 2 1 2 8 2 0
  //   1 8 2 5*1 2 3 8 1 0 0 0 1 8 2 1 1
  //   contents of rom_6 (hex, n*v repeats v):
  //   0 1 8 8 1 0 1 1 2 3 4 3 2 0 1 8 8 8 4 8 2 0 1 1 3 8 4 8 2 0 0 0 2 2 3 1 1 0 0 0 1 8 1 5*0 1 1 1 0 1
  //   1 1 5*0 1 8 1 0 0 1 8 2 1 0 0 0 1 2 3 8 1 0 0 0 1 8 2 1 2 1 2 1 2 2 2 0 2 8 3 8 1 8 1 1 3 8 3 5*1 8
  //   2 2 1 0 0 0 1 2 2 2 8 4*0 1 8 2 1 2 8 2 1 1 2 1 1 3 8 3 1 8 2 8 1 2 8 2 1 1 2 5*1 0 1 1 1 0 1 1 0 0
  //   1 8 1 0 8 2 1 1 2 2 2 0 2 3 8 1 1 8 1 0 1 8 2 4*1 0 1 1 0 0 1 8 8 1 8 2 1 0 1 2 2 1 2 8 2 1 1 0 4*1
  //   2 8 1 0 1 8 1 1 2 1 1 0 1 1 1 8 1 0 1 1 2 1 1 2 2 1 1 8 2 8 0 1 8 1 1 1 2 1
  //   contents of rom_7 (hex, n*v repeats v):
  //   8 8 1 5*0 2 2 2 1 1 5*0 1 8 2 1 1 0 1 1 2 1 2 8 1 0 1 8 1 1 2 2 1 0 2 2 1 1 8 2 2 2 8 1 0 1 2 3 8 8
  //   1 1 0 0 1 8 3 2 1 2 3 8 1 0 0 0 2 8 8 3 2 1 0 0 2 8 3 2 8 1 0 0 1 2 2 2 1 1 0 0 0 1 8 4*1 0 0 1 2 2
  //   3 8 2 0 0 0 2 8 4 8 2 0 0 0 2 8 3 1 1 4*0 1 8 1 5*0 2 2 2 0 0 1 1 0 2 8 3 1 1 8 2 1 3 8 4 8 1 8 3 2
  //   8 3 8 2 1 1 2 8 3 3 2 1 0 0 1 1 2 8 1 5*0 1 1 1 0 0 0 1 8 8 2 2 8 1 0 1 3 3 3 8 3 2 0 0 2 8 3 2 8 1
  //   0 0 2 8 2 1 2 2 0 0 1 1 2 1 2 8 4*0 1 8 3 2 4*0 1 2 8 1 5*0 1 1 1
  //   contents of rom_8 (hex, n*v repeats v):
  //   0 0 6*1 0 0 1 8 1 1 8 1 0 0 6*1 4*0 1 1 1 0 1 2 1 1 1 8 2 1 8 2 8 1 1 2 8 1 2 3 4*2 3 2 8 1 1 8 2 8
  //   2 8 8 2 2 8 1 0 0 0 1 2 8 2 1 4*0 2 2 2 4*0 1 2 8 2 1 1 0 0 8 2 2 3 8 2 1 0 2 2 3 8 4 8 1 0 1 8 3 8
  //   3 1 1 0 1 1 2 1 1 4*0 1 8 8 1 4*0 1 3 3 2 5*0 1 8 1 0 0 0 1 1 2 1 2 1 2 1 1 8 1 1 2 8 2 8 2 2 3 2 8
  //   2 2 1 1 8 3 8 2 1 0 0 1 2 8 2 1 4*0 1 8 1 0 0 1 1 0 2 2 3 1 1 1 8 0 1 8 2 8 2 2 1 0 1 1 2 3 8 2 5*0
  //   2 8 3 1 1 1 0 0 1 2 8 1 8 2 0 0 0 1 2 2 8 2 4*0 1 8
endmodule

module controller (
  input  IAck,
  input  clk,
  input  left,
  input  right,
  input  up,
  input  down,
  input  open,
  input  reset,
  input  flag,
  input  start,
  input  win,
  input  lose,
  output [2:0] vec,
  output IRQ
);

  wire and_1_out, arbiter_1_iack_2, arbiter_1_vec, arbiter_2_iack_2, arbiter_2_ireq_2, arbiter_2_vec,
       arbiter_3_iack_2, arbiter_3_ireq_2, arbiter_3_vec, arbiter_4_iack_2, arbiter_4_ireq_2, arbiter_4_vec,
       arbiter_5_iack_2, arbiter_5_ireq_2, arbiter_5_vec, arbiter_6_iack_2, arbiter_6_ireq_2, arbiter_6_vec,
       arbiter_7_ireq_2, arbiter_7_vec, d_ff_2_q, d_ff_2_qn, d_ff_3_q, d_ff_3_qn, d_ff_4_q, d_ff_4_qn,
       d_ff_5_q, d_ff_5_qn, d_ff_6_q, d_ff_6_qn, d_ff_7_q, d_ff_7_qn, d_ff_8_q, d_ff_8_qn, \end , or_1_out,
       reset_t;

  or or_1 (or_1_out, reset_t, IAck);
  D_Flip_Flop d_ff_1 (.clk(reset), .D(1'b1), .Q(reset_t), .reset(start));  // open: Qn, preset, en
  or or_2 (\end , win, lose);
  assign vec = arbiter_1_vec ? 3'b000 : 3'bz;  // Controlled_Buffer controlled_buffer_1
  D_Flip_Flop d_ff_2 (.clk(left), .D(and_1_out), .Q(d_ff_2_q), .Qn(d_ff_2_qn), .reset(or_1_out));  // open: preset, en
  and and_1 (and_1_out, 1'b1, ~\end );  // AND_Gate
  assign vec = arbiter_2_vec ? 3'b001 : 3'bz;  // Controlled_Buffer controlled_buffer_2
  arbiter arbiter_1 (
    .IReq_2(IRQ), .IAck(IAck), .IReq(arbiter_2_ireq_2), .IAck_2(arbiter_1_iack_2), .vec(arbiter_1_vec),
    .req(d_ff_2_q), .done(d_ff_2_qn), .clock(clk));
  arbiter arbiter_2 (
    .IReq_2(arbiter_2_ireq_2), .IAck(arbiter_1_iack_2), .IReq(arbiter_3_ireq_2), .IAck_2(arbiter_2_iack_2),
    .vec(arbiter_2_vec), .req(d_ff_3_q), .done(d_ff_3_qn), .clock(clk));
  D_Flip_Flop d_ff_3 (.clk(right), .D(and_1_out), .Q(d_ff_3_q), .Qn(d_ff_3_qn), .reset(or_1_out));  // open: preset, en
  assign vec = arbiter_3_vec ? 3'b010 : 3'bz;  // Controlled_Buffer controlled_buffer_3
  arbiter arbiter_3 (
    .IReq_2(arbiter_3_ireq_2), .IAck(arbiter_2_iack_2), .IReq(arbiter_4_ireq_2), .IAck_2(arbiter_3_iack_2),
    .vec(arbiter_3_vec), .req(d_ff_4_q), .done(d_ff_4_qn), .clock(clk));
  D_Flip_Flop d_ff_4 (.clk(up), .D(and_1_out), .Q(d_ff_4_q), .Qn(d_ff_4_qn), .reset(or_1_out));  // open: preset, en
  D_Flip_Flop d_ff_5 (.clk(down), .D(and_1_out), .Q(d_ff_5_q), .Qn(d_ff_5_qn), .reset(or_1_out));  // open: preset, en
  assign vec = arbiter_6_vec ? 3'b100 : 3'bz;  // Controlled_Buffer controlled_buffer_4
  assign vec = arbiter_4_vec ? 3'b011 : 3'bz;  // Controlled_Buffer controlled_buffer_5
  arbiter arbiter_4 (
    .IReq_2(arbiter_4_ireq_2), .IAck(arbiter_3_iack_2), .IReq(arbiter_6_ireq_2), .IAck_2(arbiter_4_iack_2),
    .vec(arbiter_4_vec), .req(d_ff_5_q), .done(d_ff_5_qn), .clock(clk));
  D_Flip_Flop d_ff_6 (.clk(open), .D(and_1_out), .Q(d_ff_6_q), .Qn(d_ff_6_qn), .reset(or_1_out));  // open: preset, en
  assign vec = arbiter_5_vec ? 3'b101 : 3'bz;  // Controlled_Buffer controlled_buffer_6
  arbiter arbiter_5 (
    .IReq_2(arbiter_5_ireq_2), .IAck(arbiter_6_iack_2), .IReq(arbiter_7_ireq_2), .IAck_2(arbiter_5_iack_2),
    .vec(arbiter_5_vec), .req(d_ff_7_q), .done(d_ff_7_qn), .clock(clk));
  arbiter arbiter_6 (
    .IReq_2(arbiter_6_ireq_2), .IAck(arbiter_4_iack_2), .IReq(arbiter_5_ireq_2), .IAck_2(arbiter_6_iack_2),
    .vec(arbiter_6_vec), .req(d_ff_6_q), .done(d_ff_6_qn), .clock(clk));
  D_Flip_Flop d_ff_7 (.clk(flag), .D(and_1_out), .Q(d_ff_7_q), .Qn(d_ff_7_qn), .reset(or_1_out));  // open: preset, en
  assign vec = arbiter_7_vec ? 3'b110 : 3'bz;  // Controlled_Buffer controlled_buffer_7
  arbiter arbiter_7 (
    .IReq_2(arbiter_7_ireq_2), .IAck(arbiter_5_iack_2), .IReq(1'b0), .vec(arbiter_7_vec), .req(d_ff_8_q),
    .done(d_ff_8_qn), .clock(clk));  // open: IAck_2
  D_Flip_Flop d_ff_8 (.clk(reset), .D(1'b1), .Q(d_ff_8_q), .Qn(d_ff_8_qn), .reset(IAck));  // open: preset, en

  // Other names for the same wires on the sheet: raw_reset = reset
endmodule

module cell_drawer (
  input  selected,
  input  flag,
  input  open,
  input  [7:0] cell_data,
  input  clk,
  input  force_open,
  input  reset,
  output empty,
  output [6:0] row_0,
  output [6:0] row_1,
  output [6:0] row_2,
  output [6:0] row_3,
  output [6:0] row_4,
  output [6:0] row_5,
  output [6:0] row_6,
  output [6:0] row_7
);

  wire and_1_out, and_2_out, and_5_out, is_flag, not_1_out, or_1_out;
  wire [1:0] and_3_out, or_2_out;
  wire [3:0] print;
  wire [6:0] not_2_out, not_3_out, not_4_out, not_5_out, not_6_out, not_7_out, not_8_out, not_9_out, row_0_t,
       row_1_t, row_2_t, row_3_t, row_4_t, row_5_t, row_6_t, row_7_t;
  wire [6:6] d_ff_1_q;
  wire [7:0] cell_data_t, register_1_q;

  and and_1 (and_1_out, ~cell_data_t[3], force_open);  // AND_Gate
  not not_1 (not_1_out, cell_data_t[3]);
  ROM #(.addrWidth(4), .dataWidth(7)) rom_1 (.addr(print), .data(row_0_t), .sel(1'b1));
  ROM #(.addrWidth(4), .dataWidth(7)) rom_2 (.addr(print), .data(row_1_t), .sel(1'b1));
  or or_1 (or_1_out, and_1_out, and_2_out);
  and and_2 (and_2_out, selected, open);
  and and_3 (and_3_out[0], cell_data_t[3], cell_data_t[6]);
  and and_4 (and_3_out[1], not_1_out, cell_data_t[6]);
  T_Flip_Flop t_ff_1 (.clk(flag), .T(selected), .Q(is_flag), .reset(reset));  // open: Qn, preset, en
  and and_5 (and_5_out, or_1_out, ~is_flag);  // AND_Gate
  D_Flip_Flop d_ff_1 (.clk(and_5_out), .D(1'b1), .Q(d_ff_1_q[6]), .reset(reset));  // open: Qn, preset, en
  // Probe on print
  Multiplexer #(.select(2), .width(4), .enable("false")) multiplexer_1 (
    .in0(4'b1000), .in1(4'b1001), .in2({1'b0, cell_data_t[2:0]}), .in3(4'b1010), .out(print), .sel(or_2_out));
  assign or_2_out = and_3_out | {2{cell_data_t[4]}};  // OR_Gate or_2, 2 bits wide
  Register register_1 (.D(cell_data), .Q(register_1_q), .clk(clk), .clr(reset));  // open: en
  ROM #(.addrWidth(4), .dataWidth(7)) rom_3 (.addr(print), .data(row_2_t), .sel(1'b1));
  ROM #(.addrWidth(4), .dataWidth(7)) rom_4 (.addr(print), .data(row_3_t), .sel(1'b1));
  assign cell_data_t = {3'b000, is_flag, 4'b0000} | {1'b0, d_ff_1_q[6], {6{1'b0}}} | register_1_q;  // OR_Gate or_3, 8 bits wide
  // Probe on cell_data_t
  Pull_Resistor pull_resistor_1 (.node(cell_data_t[1]));
  Pull_Resistor pull_resistor_2 (.node(cell_data_t[2]));
  Pull_Resistor pull_resistor_3 (.node(cell_data_t[3]));
  ROM #(.addrWidth(4), .dataWidth(7)) rom_5 (.addr(print), .data(row_4_t), .sel(1'b1));
  ROM #(.addrWidth(4), .dataWidth(7)) rom_6 (.addr(print), .data(row_5_t), .sel(1'b1));
  Pull_Resistor pull_resistor_4 (.node(cell_data_t[0]));
  nor nor_1 (empty, cell_data_t[0], cell_data_t[1], cell_data_t[2], cell_data_t[3]);
  ROM #(.addrWidth(4), .dataWidth(7)) rom_7 (.addr(print), .data(row_6_t), .sel(1'b1));
  ROM #(.addrWidth(4), .dataWidth(7)) rom_8 (.addr(print), .data(row_7_t), .sel(1'b1));
  Pull_Resistor pull_resistor_5 (.node(selected));
  Multiplexer #(.width(7), .enable("false")) multiplexer_2 (
    .in0(row_0_t), .in1(not_2_out), .out(row_0), .sel(selected));
  assign not_2_out = ~row_0_t;  // NOT_Gate not_2, 7 bits wide
  Multiplexer #(.width(7), .enable("false")) multiplexer_3 (
    .in0(row_1_t), .in1(not_3_out), .out(row_1), .sel(selected));
  assign not_3_out = ~row_1_t;  // NOT_Gate not_3, 7 bits wide
  Multiplexer #(.width(7), .enable("false")) multiplexer_4 (
    .in0(row_2_t), .in1(not_4_out), .out(row_2), .sel(selected));
  assign not_4_out = ~row_2_t;  // NOT_Gate not_4, 7 bits wide
  Multiplexer #(.width(7), .enable("false")) multiplexer_5 (
    .in0(row_3_t), .in1(not_5_out), .out(row_3), .sel(selected));
  assign not_5_out = ~row_3_t;  // NOT_Gate not_5, 7 bits wide
  Multiplexer #(.width(7), .enable("false")) multiplexer_6 (
    .in0(row_4_t), .in1(not_6_out), .out(row_4), .sel(selected));
  assign not_6_out = ~row_4_t;  // NOT_Gate not_6, 7 bits wide
  Multiplexer #(.width(7), .enable("false")) multiplexer_7 (
    .in0(row_5_t), .in1(not_7_out), .out(row_5), .sel(selected));
  assign not_7_out = ~row_5_t;  // NOT_Gate not_7, 7 bits wide
  Multiplexer #(.width(7), .enable("false")) multiplexer_8 (
    .in0(row_6_t), .in1(not_8_out), .out(row_6), .sel(selected));
  assign not_8_out = ~row_6_t;  // NOT_Gate not_8, 7 bits wide
  Multiplexer #(.width(7), .enable("false")) multiplexer_9 (
    .in0(row_7_t), .in1(not_9_out), .out(row_7), .sel(selected));
  assign not_9_out = ~row_7_t;  // NOT_Gate not_9, 7 bits wide
  DotMatrix #(.matrixcols(8)) dotmatrix_1 (
    .col0(row_0), .col1(row_1), .col2(row_2), .col3(row_3), .col4(row_4), .col5(row_5), .col6(row_6),
    .col7(row_7));

  // Notes on the sheet:
  //   contents of rom_2 (hex, n*v repeats v):
  //   8*0 3e 22
  //   contents of rom_3 (hex, n*v repeats v):
  //   0 0 26 22 c 3a 1c 0 3e 8 3e
  //   contents of rom_4 (hex, n*v repeats v):
  //   0 20 2a 2a 14 2a 2a 0 3e 1c 38
  //   contents of rom_5 (hex, n*v repeats v):
  //   0 3e 2a 2a 3e 2a 2a 0 3e 1c 38
  //   contents of rom_6 (hex, n*v repeats v):
  //   0 0 12 14 4 24 4 0 3e 8 38
  //   contents of rom_7 (hex, n*v repeats v):
  //   8*0 3e 22
endmodule

module row_drawer (
  input  clk,
  input  selected,
  input  [2:0] selected_cell,
  input  left,
  input  right,
  input  open,
  input  flag,
  input  reset,
  input  [31:0] data,
  input  [7:0] force_in,
  output [6:0] _00,
  output [6:0] _40,
  output [6:0] _01,
  output [6:0] _41,
  output [6:0] _02,
  output [6:0] _42,
  output [6:0] _03,
  output [6:0] _43,
  output [6:0] _04,
  output [6:0] _44,
  output [6:0] _05,
  output [6:0] _45,
  output [6:0] _06,
  output [6:0] _46,
  output [6:0] _07,
  output [6:0] _47,
  output [6:0] _10,
  output [6:0] _50,
  output [6:0] _11,
  output [6:0] _51,
  output [6:0] _12,
  output [6:0] _52,
  output [6:0] _13,
  output [6:0] _53,
  output [6:0] _14,
  output [6:0] _54,
  output [6:0] _15,
  output [6:0] _55,
  output [6:0] _16,
  output [6:0] _56,
  output [6:0] _17,
  output [6:0] _57,
  output [6:0] _20,
  output [6:0] _60,
  output [6:0] _21,
  output [6:0] _61,
  output [6:0] _22,
  output [6:0] _62,
  output [6:0] _23,
  output [6:0] _63,
  output [6:0] _24,
  output [6:0] _64,
  output [6:0] _25,
  output [6:0] _65,
  output [6:0] _26,
  output [6:0] _66,
  output [6:0] _27,
  output [6:0] _67,
  output [6:0] _30,
  output [6:0] _70,
  output [6:0] _31,
  output [6:0] _71,
  output [6:0] _32,
  output [6:0] _72,
  output [6:0] _33,
  output [6:0] _73,
  output [6:0] _34,
  output [6:0] _74,
  output [6:0] _35,
  output [6:0] _75,
  output [6:0] _36,
  output [6:0] _76,
  output [6:0] _37,
  output [6:0] _77,
  output [7:0] force_out
);

  wire and_1_out, and_2_out, and_3_out, and_5_out, and_6_out, and_7_out, and_9_out, and_10_out, and_11_out,
       and_13_out, and_14_out, and_15_out, and_17_out, and_18_out, and_19_out, and_21_out, and_22_out,
       and_23_out, and_24_out, and_26_out, and_27_out, and_28_out, and_30_out, and_31_out, d_ff_1_q,
       d_ff_2_q, d_ff_3_q, d_ff_4_q, d_ff_5_q, d_ff_6_q, d_ff_7_q, d_ff_8_q, empty_0, empty_1, empty_2,
       empty_3, empty_4, empty_5, empty_6, empty_7, force_0, force_1, force_2, force_3, force_4, force_5,
       force_6, force_7, or_1_out, or_3_out, or_5_out, or_7_out, or_9_out, or_11_out, or_13_out, or_15_out,
       selected_0, selected_1, selected_2, selected_3, selected_4, selected_5, selected_6, selected_7;

  Demultiplexer #(.select(3), .enable("false")) demultiplexer_1 (
    .out0(selected_0), .out1(selected_1), .out2(selected_2), .out3(selected_3), .out4(selected_4),
    .out5(selected_5), .out6(selected_6), .out7(selected_7), .in(selected), .sel(selected_cell));
  and and_1 (and_1_out, left, clk);
  cell_drawer cell_drawer_1 (
    .cell_data(data[7:0]), .row_0(_00), .row_1(_01), .row_2(_02), .row_3(_03), .row_4(_04), .row_5(_05),
    .row_6(_06), .row_7(_07), .selected(selected_0), .flag(flag), .open(open), .clk(and_1_out),
    .empty(empty_0), .force_open(force_0), .reset(reset));
  cell_drawer cell_drawer_2 (
    .cell_data(data[15:8]), .row_0(_10), .row_1(_11), .row_2(_12), .row_3(_13), .row_4(_14), .row_5(_15),
    .row_6(_16), .row_7(_17), .selected(selected_1), .flag(flag), .open(open), .clk(and_1_out),
    .empty(empty_1), .force_open(force_1), .reset(reset));
  cell_drawer cell_drawer_3 (
    .cell_data(data[23:16]), .row_0(_20), .row_1(_21), .row_2(_22), .row_3(_23), .row_4(_24), .row_5(_25),
    .row_6(_26), .row_7(_27), .selected(selected_2), .flag(flag), .open(open), .clk(and_1_out),
    .empty(empty_2), .force_open(force_2), .reset(reset));
  cell_drawer cell_drawer_4 (
    .cell_data(data[31:24]), .row_0(_30), .row_1(_31), .row_2(_32), .row_3(_33), .row_4(_34), .row_5(_35),
    .row_6(_36), .row_7(_37), .selected(selected_3), .flag(flag), .open(open), .clk(and_1_out),
    .empty(empty_3), .force_open(force_3), .reset(reset));
  and and_2 (and_2_out, open, selected_7);
  or or_1 (or_1_out, and_2_out, force_in[7], force_in[6]);
  and and_3 (and_3_out, empty_6, d_ff_2_q);
  or or_2 (force_7, or_1_out, and_3_out);
  D_Flip_Flop d_ff_1 (.clk(force_7), .D(force_7), .Q(d_ff_1_q), .reset(reset));  // open: Qn, preset, en
  and and_4 (force_out[7], d_ff_1_q, empty_7);
  and and_5 (and_5_out, open, selected_6);
  or or_3 (or_3_out, and_5_out, force_in[7], force_in[6], force_in[5]);
  and and_6 (and_6_out, empty_5, d_ff_3_q);
  and and_7 (and_7_out, empty_7, d_ff_1_q);
  or or_4 (force_6, and_7_out, or_3_out, and_6_out);
  D_Flip_Flop d_ff_2 (.clk(force_6), .D(force_6), .Q(d_ff_2_q), .reset(reset));  // open: Qn, preset, en
  and and_8 (force_out[6], d_ff_2_q, empty_6);
  and and_9 (and_9_out, open, selected_5);
  or or_5 (or_5_out, and_9_out, force_in[6], force_in[5], force_in[4]);
  and and_10 (and_10_out, empty_6, d_ff_2_q);
  and and_11 (and_11_out, empty_4, d_ff_4_q);
  or or_6 (force_5, and_10_out, or_5_out, and_11_out);
  D_Flip_Flop d_ff_3 (.clk(force_5), .D(force_5), .Q(d_ff_3_q), .reset(reset));  // open: Qn, preset, en
  and and_12 (force_out[5], d_ff_3_q, empty_5);
  and and_13 (and_13_out, open, selected_4);
  or or_7 (or_7_out, and_13_out, force_in[5], force_in[4], force_in[3]);
  and and_14 (and_14_out, empty_5, d_ff_3_q);
  and and_15 (and_15_out, empty_3, d_ff_5_q);
  or or_8 (force_4, and_14_out, or_7_out, and_15_out);
  D_Flip_Flop d_ff_4 (.clk(force_4), .D(force_4), .Q(d_ff_4_q), .reset(reset));  // open: Qn, preset, en
  and and_16 (force_out[4], d_ff_4_q, empty_4);
  or or_9 (or_9_out, force_in[4], force_in[3], force_in[1], and_19_out);
  and and_17 (and_17_out, empty_4, d_ff_4_q);
  and and_18 (and_18_out, empty_2, d_ff_6_q);
  or or_10 (force_3, and_17_out, or_9_out, and_18_out);
  and and_19 (and_19_out, open, selected_3);
  D_Flip_Flop d_ff_5 (.clk(force_3), .D(force_3), .Q(d_ff_5_q), .reset(reset));  // open: Qn, preset, en
  and and_20 (force_out[3], empty_3, d_ff_5_q);
  and and_21 (and_21_out, clk, right);
  or or_11 (or_11_out, force_in[3], force_in[2], force_in[1], and_23_out);
  and and_22 (and_22_out, empty_3, d_ff_5_q);
  or or_12 (force_2, and_22_out, or_11_out, and_24_out);
  cell_drawer cell_drawer_5 (
    .cell_data(data[7:0]), .row_0(_40), .row_1(_41), .row_2(_42), .row_3(_43), .row_4(_44), .row_5(_45),
    .row_6(_46), .row_7(_47), .selected(selected_4), .flag(flag), .open(open), .clk(and_21_out),
    .empty(empty_4), .force_open(force_4), .reset(reset));
  cell_drawer cell_drawer_6 (
    .cell_data(data[15:8]), .row_0(_50), .row_1(_51), .row_2(_52), .row_3(_53), .row_4(_54), .row_5(_55),
    .row_6(_56), .row_7(_57), .selected(selected_5), .flag(flag), .open(open), .clk(and_21_out),
    .empty(empty_5), .force_open(force_5), .reset(reset));
  cell_drawer cell_drawer_7 (
    .cell_data(data[23:16]), .row_0(_60), .row_1(_61), .row_2(_62), .row_3(_63), .row_4(_64), .row_5(_65),
    .row_6(_66), .row_7(_67), .selected(selected_6), .flag(flag), .open(open), .clk(and_21_out),
    .empty(empty_6), .force_open(force_6), .reset(reset));
  cell_drawer cell_drawer_8 (
    .cell_data(data[31:24]), .row_0(_70), .row_1(_71), .row_2(_72), .row_3(_73), .row_4(_74), .row_5(_75),
    .row_6(_76), .row_7(_77), .selected(selected_7), .flag(flag), .open(open), .clk(and_21_out),
    .empty(empty_7), .force_open(force_7), .reset(reset));
  and and_23 (and_23_out, open, selected_2);
  and and_24 (and_24_out, empty_1, d_ff_7_q);
  D_Flip_Flop d_ff_6 (.clk(force_2), .D(force_2), .Q(d_ff_6_q), .reset(reset));  // open: Qn, preset, en
  and and_25 (force_out[2], empty_2, d_ff_6_q);
  and and_26 (and_26_out, empty_2, d_ff_6_q);
  and and_27 (and_27_out, open, selected_1);
  or or_13 (or_13_out, force_in[2], force_in[1], force_in[0], and_27_out);
  and and_28 (and_28_out, empty_0, d_ff_8_q);
  or or_14 (force_1, and_26_out, or_13_out, and_28_out);
  D_Flip_Flop d_ff_7 (.clk(force_1), .D(force_1), .Q(d_ff_7_q), .reset(reset));  // open: Qn, preset, en
  and and_29 (force_out[1], empty_1, d_ff_7_q);
  and and_30 (and_30_out, open, selected_0);
  and and_31 (and_31_out, empty_1, d_ff_7_q);
  or or_15 (or_15_out, force_in[1], force_in[0], and_30_out);
  or or_16 (force_0, and_31_out, or_15_out);
  D_Flip_Flop d_ff_8 (.clk(force_0), .D(force_0), .Q(d_ff_8_q), .reset(reset));  // open: Qn, preset, en
  and and_32 (force_out[0], empty_0, d_ff_8_q);
endmodule

module video_handler (
  input  [3:0] row_num,
  input  clk,
  input  [7:0] selected,
  output clk_0,
  output clk_1,
  output clk_2,
  output clk_3,
  output clk_4,
  output clk_5,
  output clk_6,
  output clk_7,
  output left_clk,
  output clk_0_2,
  output right_clk,
  output clk_1_2,
  output clk_2_2,
  output clk_3_2,
  output clk_4_2,
  output clk_5_2,
  output clk_6_2,
  output clk_7_2,
  output [2:0] selected_col
);

  wire [3:0] divider_1_out, divider_1_rem;
  wire [7:0] divider_2_out;
  wire [7:3] divider_2_rem;

  Demultiplexer #(.enable("false")) demultiplexer_1 (
    .out0(left_clk), .out1(right_clk), .in(1'b1), .sel(divider_1_rem[0]));
  Divider #(.width(4)) divider_1 (.a(row_num), .b(4'b0010), .out(divider_1_out), .rem(divider_1_rem));  // open: upper
  // Probe on selected
  Demultiplexer #(.select(3), .enable("false")) demultiplexer_2 (
    .out0(clk_0), .out1(clk_1), .out2(clk_2), .out3(clk_3), .out4(clk_4), .out5(clk_5), .out6(clk_6),
    .out7(clk_7), .in(clk), .sel(divider_1_out[2:0]));
  Divider divider_2 (.a(selected), .b(8'h8), .out(divider_2_out), .rem({divider_2_rem, selected_col}));  // open: upper
  Demultiplexer #(.select(3), .enable("false")) demultiplexer_3 (
    .out0(clk_0_2), .out1(clk_1_2), .out2(clk_2_2), .out3(clk_3_2), .out4(clk_4_2), .out5(clk_5_2),
    .out6(clk_6_2), .out7(clk_7_2), .in(1'b1), .sel(divider_2_out[2:0]));
endmodule

module map_loader (
  input  clk,
  input  reset,
  output loaded,
  output [7:0] data,
  output [7:0] addr
);

  wire and_1_out, and_2_out, and_3_out, not_1_out, not_2_out, not_3_out, or_1_out, t_ff_1_q, t_ff_2_q;

  and and_1 (and_1_out, ~loaded, clk);  // AND_Gate
  T_Flip_Flop t_ff_1 (.clk(and_2_out), .T(and_2_out), .Q(t_ff_1_q), .reset(not_1_out));  // open: Qn, preset, en
  not not_1 (not_1_out, reset);
  and and_2 (and_2_out, t_ff_2_q, ~t_ff_1_q);  // AND_Gate
  Counter counter_1 (.Q(addr), .clk(or_1_out), .clr(and_3_out));  // open: load, D, count, carry
  buf or_1 (or_1_out, and_1_out);  // OR_Gate
  not not_2 (not_2_out, reset);
  and and_3 (and_3_out, reset, ~t_ff_2_q);  // AND_Gate
  map_selector map_selector_1 (.addr(addr), .sel(not_3_out), .clk(reset), .cell_info(data));
  not not_3 (not_3_out, loaded);
  Pull_Resistor pull_resistor_1 (.node(data));
  Comparator comparator_1 (.a(addr), .b(8'h41), .eq(loaded));  // open: gt, lt
  T_Flip_Flop t_ff_2 (.clk(and_3_out), .T(and_3_out), .Q(t_ff_2_q), .reset(not_2_out));  // open: Qn, preset, en
endmodule

module delayer (
  input  bus_0,
  output first,
  output second
);

  wire not_1_out;

  and and_1 (first, ~second, bus_0);  // AND_Gate
  not not_1 (not_1_out, bus_0);
  T_Flip_Flop t_ff_1 (.clk(first), .T(first), .Q(second), .reset(not_1_out));  // open: Qn, preset, en
endmodule

module Info_display (
  input  win,
  input  lose,
  input  reset,
  input  start,
  input  [7:0] flags,
  output [13:0] _00,
  output [13:0] _00_2,
  output [13:0] _00_3,
  output [13:0] _00_4,
  output [13:0] _00_5,
  output [13:0] _01,
  output [13:0] _01_2,
  output [13:0] _01_3,
  output [13:0] _01_4,
  output [13:0] _01_5,
  output [13:0] _00_6,
  output [13:0] _00_7,
  output [13:0] _00_8,
  output [13:0] _00_9,
  output [13:0] _00_10,
  output [13:0] _01_6,
  output [13:0] _01_7,
  output [13:0] _01_8,
  output [13:0] _01_9,
  output [13:0] _01_10,
  output [13:0] _00_11,
  output [13:0] _00_12,
  output [13:0] _00_13,
  output [13:0] _00_14,
  output [13:0] _00_15,
  output [13:0] _01_11,
  output [13:0] _01_12,
  output [13:0] _01_13,
  output [13:0] _01_14,
  output [13:0] _01_15,
  output [13:0] _00_16,
  output [13:0] _00_17,
  output [13:0] _00_18,
  output [13:0] _00_19,
  output [13:0] _00_20,
  output [13:0] _01_16,
  output [13:0] _01_17,
  output [13:0] _01_18,
  output [13:0] _01_19,
  output [13:0] _01_20
);

  wire button_1_out, button_2_out, comparator_1_eq, comparator_2_eq, comparator_3_gt, comparator_4_eq, \end ,
       inited, lose_t, or_1_out, or_4_out, playing, reset_print_bot, reset_print_top, reset_t;
  wire [7:0] adder_1_out, cell_0, cell_1, cell_2, cell_3, cell_4, cell_5, cell_6, cell_7, cell_8, cell_9,
       mines_left, mines_right, multiplexer_2_out, multiplexer_3_out;

  Button button_1 (.out(button_1_out));
  or or_1 (or_1_out, start, button_2_out);
  Button button_2 (.out(button_2_out));
  or or_2 (reset_print_top, ~inited, reset_t);  // OR_Gate
  nor nor_1 (reset_print_bot, reset_t, inited);
  and and_1 (playing, ~\end , ~reset_t, inited);  // AND_Gate
  Multiplexer #(.width(8)) multiplexer_1 (
    .in0({8{1'b0}}), .in1(8'h1), .out(mines_left), .sel(comparator_1_eq), .en(playing));
  Comparator comparator_1 (.a(flags), .b(8'ha), .eq(comparator_1_eq));  // open: gt, lt
  Multiplexer #(.width(8)) multiplexer_2 (
    .in0(flags), .in1({8{1'b0}}), .out(multiplexer_2_out), .sel(comparator_2_eq), .en(playing));
  Comparator comparator_2 (.a(flags), .b(8'ha), .eq(comparator_2_eq));  // open: gt, lt
  or or_3 (\end , win, lose);
  D_Flip_Flop d_ff_1 (.clk(or_4_out), .D(or_4_out), .Q(inited));  // open: Qn, preset, en, reset
  or or_4 (or_4_out, reset, button_1_out);
  D_Flip_Flop d_ff_2 (.clk(or_4_out), .D(or_4_out), .Q(reset_t), .reset(or_1_out));  // open: Qn, preset, en
  // Probe on multiplexer_2_out
  Comparator comparator_3 (.a(multiplexer_2_out), .b(8'h7), .gt(comparator_3_gt));  // open: eq, lt
  symb_drawer symb_drawer_1 (
    .symb(cell_0), .row_0(_00_5[13:7]), .row_0_2(_01_5[13:7]), .row_0_3(_00_10[13:7]),
    .row_0_4(_01_10[13:7]), .row_0_5(_00_15[13:7]), .row_0_6(_01_15[13:7]), .row_0_7(_00_20[13:7]),
    .row_0_8(_01_20[13:7]));
  assign cell_0 = \end  ? 8'h23 : 8'bz;  // Controlled_Buffer controlled_buffer_1
  assign cell_5 = lose_t ? 8'h16 : 8'bz;  // Controlled_Buffer controlled_buffer_2
  assign cell_5 = win ? 8'h21 : 8'bz;  // Controlled_Buffer controlled_buffer_3
  // Probe on adder_1_out
  Adder adder_1 (.a(multiplexer_2_out), .b(multiplexer_3_out), .out(adder_1_out));  // open: cin, cout
  Multiplexer #(.width(8), .enable("false")) multiplexer_3 (
    .in0({8{1'b0}}), .in1(8'h1d), .out(multiplexer_3_out), .sel(comparator_3_gt));
  assign cell_0 = reset_print_top ? 8'h1a : 8'bz;  // Controlled_Buffer controlled_buffer_4
  assign cell_0 = playing ? mines_left : 8'bz;  // Controlled_Buffer controlled_buffer_5
  assign cell_5 = playing ? 8'h10 : 8'bz;  // Controlled_Buffer controlled_buffer_6
  Comparator comparator_4 (.a({8{1'b0}}), .b(adder_1_out), .eq(comparator_4_eq));  // open: gt, lt
  symb_drawer symb_drawer_2 (
    .symb(cell_5), .row_0(_00_5[6:0]), .row_0_2(_01_5[6:0]), .row_0_3(_00_10[6:0]), .row_0_4(_01_10[6:0]),
    .row_0_5(_00_15[6:0]), .row_0_6(_01_15[6:0]), .row_0_7(_00_20[6:0]), .row_0_8(_01_20[6:0]));
  assign cell_5 = reset_print_bot ? 8'h1c : 8'bz;  // Controlled_Buffer controlled_buffer_7
  assign cell_5 = reset_t ? 8'h1d : 8'bz;  // Controlled_Buffer controlled_buffer_8
  // Probe on mines_right
  Multiplexer #(.width(8), .enable("false")) multiplexer_4 (
    .in0(adder_1_out), .in1(8'h19), .out(mines_right), .sel(comparator_4_eq));
  assign cell_1 = \end  ? 8'h19 : 8'bz;  // Controlled_Buffer controlled_buffer_9
  symb_drawer symb_drawer_3 (
    .symb(cell_1), .row_0(_00[13:7]), .row_0_2(_01[13:7]), .row_0_3(_00_6[13:7]), .row_0_4(_01_6[13:7]),
    .row_0_5(_00_11[13:7]), .row_0_6(_01_11[13:7]), .row_0_7(_00_16[13:7]), .row_0_8(_01_16[13:7]));
  assign cell_1 = playing ? mines_right : 8'bz;  // Controlled_Buffer controlled_buffer_10
  assign cell_6 = lose_t ? 8'h19 : 8'bz;  // Controlled_Buffer controlled_buffer_11
  assign cell_6 = win ? 8'h13 : 8'bz;  // Controlled_Buffer controlled_buffer_12
  assign cell_1 = reset_print_top ? 8'h1c : 8'bz;  // Controlled_Buffer controlled_buffer_13
  assign cell_6 = playing ? 8'h16 : 8'bz;  // Controlled_Buffer controlled_buffer_14
  assign cell_6 = reset_t ? 8'h1e : 8'bz;  // Controlled_Buffer controlled_buffer_15
  symb_drawer symb_drawer_4 (
    .symb(cell_6), .row_0(_00[6:0]), .row_0_2(_01[6:0]), .row_0_3(_00_6[6:0]), .row_0_4(_01_6[6:0]),
    .row_0_5(_00_11[6:0]), .row_0_6(_01_11[6:0]), .row_0_7(_00_16[6:0]), .row_0_8(_01_16[6:0]));
  assign cell_2 = \end  ? 8'h1f : 8'bz;  // Controlled_Buffer controlled_buffer_16
  assign cell_6 = reset_print_bot ? 8'hf : 8'bz;  // Controlled_Buffer controlled_buffer_17
  assign cell_2 = reset_print_top ? 8'hf : 8'bz;  // Controlled_Buffer controlled_buffer_18
  assign cell_2 = playing ? 8'ha : 8'bz;  // Controlled_Buffer controlled_buffer_19
  assign cell_7 = lose_t ? 8'h1d : 8'bz;  // Controlled_Buffer controlled_buffer_20
  symb_drawer symb_drawer_5 (
    .symb(cell_2), .row_0(_00_2[13:7]), .row_0_2(_01_2[13:7]), .row_0_3(_00_7[13:7]), .row_0_4(_01_7[13:7]),
    .row_0_5(_00_12[13:7]), .row_0_6(_01_12[13:7]), .row_0_7(_00_17[13:7]), .row_0_8(_01_17[13:7]));
  assign cell_7 = win ? 8'h18 : 8'bz;  // Controlled_Buffer controlled_buffer_21
  assign cell_7 = playing ? 8'hb : 8'bz;  // Controlled_Buffer controlled_buffer_22
  assign cell_3 = reset_print_top ? 8'h1d : 8'bz;  // Controlled_Buffer controlled_buffer_23
  assign cell_7 = reset_t ? 8'hb : 8'bz;  // Controlled_Buffer controlled_buffer_24
  assign cell_7 = reset_print_bot ? 8'h1d : 8'bz;  // Controlled_Buffer controlled_buffer_25
  symb_drawer symb_drawer_6 (
    .symb(cell_7), .row_0(_00_2[6:0]), .row_0_2(_01_2[6:0]), .row_0_3(_00_7[6:0]), .row_0_4(_01_7[6:0]),
    .row_0_5(_00_12[6:0]), .row_0_6(_01_12[6:0]), .row_0_7(_00_17[6:0]), .row_0_8(_01_17[6:0]));
  assign cell_8 = playing ? 8'h11 : 8'bz;  // Controlled_Buffer controlled_buffer_26
  assign cell_8 = lose ? 8'hf : 8'bz;  // Controlled_Buffer controlled_buffer_27
  symb_drawer symb_drawer_7 (
    .symb(cell_3), .row_0(_00_3[13:7]), .row_0_2(_01_3[13:7]), .row_0_3(_00_8[13:7]), .row_0_4(_01_8[13:7]),
    .row_0_5(_00_13[13:7]), .row_0_6(_01_13[13:7]), .row_0_7(_00_18[13:7]), .row_0_8(_01_18[13:7]));
  assign cell_4 = reset_print_top ? 8'h1d : 8'bz;  // Controlled_Buffer controlled_buffer_28
  assign cell_8 = reset_print_bot ? 8'hf : 8'bz;  // Controlled_Buffer controlled_buffer_29
  assign cell_8 = reset_t ? 8'h1c : 8'bz;  // Controlled_Buffer controlled_buffer_30
  assign cell_9 = playing ? 8'h1d : 8'bz;  // Controlled_Buffer controlled_buffer_31
  symb_drawer symb_drawer_8 (
    .symb(cell_8), .row_0(_00_3[6:0]), .row_0_2(_01_3[6:0]), .row_0_3(_00_8[6:0]), .row_0_4(_01_8[6:0]),
    .row_0_5(_00_13[6:0]), .row_0_6(_01_13[6:0]), .row_0_7(_00_18[6:0]), .row_0_8(_01_18[6:0]));
  assign cell_9 = reset_t ? 8'h1e : 8'bz;  // Controlled_Buffer controlled_buffer_32
  assign cell_9 = reset_print_bot ? 8'h1e : 8'bz;  // Controlled_Buffer controlled_buffer_33
  symb_drawer symb_drawer_9 (
    .symb(cell_4), .row_0(_00_4[13:7]), .row_0_2(_01_4[13:7]), .row_0_3(_00_9[13:7]), .row_0_4(_01_9[13:7]),
    .row_0_5(_00_14[13:7]), .row_0_6(_01_14[13:7]), .row_0_7(_00_19[13:7]), .row_0_8(_01_19[13:7]));
  symb_drawer symb_drawer_10 (
    .symb(cell_9), .row_0(_00_4[6:0]), .row_0_2(_01_4[6:0]), .row_0_3(_00_9[6:0]), .row_0_4(_01_9[6:0]),
    .row_0_5(_00_14[6:0]), .row_0_6(_01_14[6:0]), .row_0_7(_00_19[6:0]), .row_0_8(_01_19[6:0]));
endmodule

module symb_drawer (
  input  [7:0] symb,
  output [6:0] row_0,
  output [6:0] row_0_2,
  output [6:0] row_0_3,
  output [6:0] row_0_4,
  output [6:0] row_0_5,
  output [6:0] row_0_6,
  output [6:0] row_0_7,
  output [6:0] row_0_8
);

  // Probe on symb
  Pull_Resistor pull_resistor_1 (.node(symb));
  ROM #(.dataWidth(7)) rom_1 (.addr(symb), .data(row_0), .sel(1'b1));
  ROM #(.dataWidth(7)) rom_2 (.addr(symb), .data(row_0_5), .sel(1'b1));
  ROM #(.dataWidth(7)) rom_3 (.addr(symb), .data(row_0_2), .sel(1'b1));
  ROM #(.dataWidth(7)) rom_4 (.addr(symb), .data(row_0_6), .sel(1'b1));
  ROM #(.dataWidth(7)) rom_5 (.addr(symb), .data(row_0_3), .sel(1'b1));
  ROM #(.dataWidth(7)) rom_6 (.addr(symb), .data(row_0_7), .sel(1'b1));
  ROM #(.dataWidth(7)) rom_7 (.addr(symb), .data(row_0_4), .sel(1'b1));
  ROM #(.dataWidth(7)) rom_8 (.addr(symb), .data(row_0_8), .sel(1'b1));

  // Other names for the same wires on the sheet: addr[7:0] = symb; data_0[6:0] = row_0; data_1[6:0] = row_0_2;
  //   data_2[6:0] = row_0_3; data_3[6:0] = row_0_4; data_4[6:0] = row_0_5; data_5[6:0] = row_0_6;
  //   data_6[6:0] = row_0_7; data_7[6:0] = row_0_8

  // Notes on the sheet:
  //   contents of rom_2 (hex, n*v repeats v):
  //   0 3e 2a 2a 3e 2a 2a 28 3e 1c 38 28 2a 22 22 2a 28 2a 8 3e 22 8 2 10 4 22 28 2a 28 2a 3e 2 2 4 8 a 2a
  //   2a 2a
  //   contents of rom_3 (hex, n*v repeats v):
  //   8*0 3e 22 0 1e 3e 1c 3e 3e 3e 1c 3e 22 4 4*3e 1c 3e 1c 3e 10 20 3c 38 3c 36 32 22 14
  //   contents of rom_4 (hex, n*v repeats v):
  //   0 0 12 14 4 24 4 30 3e 8 38 28 1a 22 0 22 28 2a 8 22 22 36 2 20 0 22 28 24 28 2a 20 2 4 2 8 a 32 2a
  //   2a
  //   contents of rom_5 (hex, n*v repeats v):
  //   0 0 26 22 c 3a 1c 20 3e 8 3e 28 2a 22 22 2a 28 22 8 22 2 8 2 20 10 22 28 22 28 2a 20 2 4 2 8 a 22 2a
  //   10
  //   contents of rom_6 (hex, n*v repeats v):
  //   8*0 3e 22 0 1e 4 14 1c 22 20 4 3e 22 3c 0 6 3e 3e 1c 10 1e 16 4 20 3c 38 3c 36 3e 22 14 1c
  //   contents of rom_7 (hex, n*v repeats v):
  //   0 20 2a 2a 14 2a 2a 26 3e 1c 38 28 2a 22 22 2a 28 22 8 3e 2 8 2 10 8 22 28 22 28 2a 3e 2 2 4 8 a 26
  //   2a 2a
endmodule
